// Logisim project ALU.circ as structural Verilog: 22 circuits, main circuit ALU
module ALU (
  input  [31:0] X,
  input  [31:0] Y,
  input  [3:0] AluOP,
  output Signed_Overflow_350b0444,
  output UnSigned_Overflow_28bd2ab2,
  output Equal,
  output [31:0] Result,
  output [31:0] Result_2_406f29fe
);

  wire and_2_out, and_3_out, and_4_out, and_5_out, n32bit_adder_1_out_4, not_1_out, not_2_out, not_3_out,
       not_4_out, not_5_out, not_6_out, or_2_out, or_3_out, sub_1_out_4;
  wire [31:0] and_1_out_3, div_1_out_3, div_1_out_4, mul_1_out_3, mul_1_out_4, n32bit_adder_1_out_5,
       nor_1_out_3, or_1_out_3, sar_1_out_3, scmp_1_out_3, shl_1_out_3, shr_1_out_3, sub_1_out_3,
       ucmp_1_out_4, xor_1_out_3;

  // Probe on X
  // Probe on X
  SAR sar_1 (.in_1(X), .in_2(Y), .out_3(sar_1_out_3));
  SHL shl_1 (.in_1(X), .in_2(Y), .out_3(shl_1_out_3));
  // Probe on Y
  // Probe on Y
  Multiplexer #(.select(4), .width(32), .enable("false")) multiplexer_1 (
    .in0(shl_1_out_3), .in1(sar_1_out_3), .in2(shr_1_out_3), .in3(mul_1_out_3), .in4(div_1_out_3),
    .in5(n32bit_adder_1_out_5), .in6(sub_1_out_3), .in7(and_1_out_3), .in8(or_1_out_3), .in9(xor_1_out_3),
    .in10(nor_1_out_3), .in11(scmp_1_out_3), .in12(ucmp_1_out_4), .in13({32{1'b0}}), .in14({32{1'b0}}),
    .in15({32{1'b0}}), .out(Result), .sel(AluOP));
  MUL mul_1 (.in_1(X), .in_2(Y), .out_3(mul_1_out_3), .out_4(mul_1_out_4));
  SHR shr_1 (.in_1(X), .in_2(Y), .out_3(shr_1_out_3));
  _32bit_adder u_32bit_adder_1 (.A(X), .B(Y), .in_1(1'b0), .out_5(n32bit_adder_1_out_5), .out_4(n32bit_adder_1_out_4));
  DIV div_1 (.in_1(X), .in_2(Y), .out_3(div_1_out_3), .out_4(div_1_out_4));
  // Probe on AluOP
  AND and_1 (.in_1(X), .in_2(Y), .out_3(and_1_out_3));
  SUB sub_1 (.out_4(sub_1_out_4), .out_3(sub_1_out_3), .X(X), .Y(Y));
  // Probe on Result
  // Probe on Result
  Multiplexer #(.select(4), .width(32), .enable("false")) multiplexer_2 (
    .in0({32{1'b0}}), .in1({32{1'b0}}), .in2({32{1'b0}}), .in3(mul_1_out_4), .in4(div_1_out_4),
    .in5({32{1'b0}}), .in6({32{1'b0}}), .in7({32{1'b0}}), .in8({32{1'b0}}), .in9({32{1'b0}}),
    .in10({32{1'b0}}), .in11({32{1'b0}}), .in12({32{1'b0}}), .in13({32{1'b0}}), .in14({32{1'b0}}),
    .in15({32{1'b0}}), .out(Result_2_406f29fe), .sel(AluOP));
  XOR xor_1 (.in_1(X), .in_2(Y), .out_3(xor_1_out_3));
  OR or_1 (.in_1(X), .in_2(Y), .out_3(or_1_out_3));
  SCMP scmp_1 (.out_3(scmp_1_out_3), .in_1(X), .in_2(Y));
  NOR nor_1 (.in_1(X), .in_2(Y), .out_3(nor_1_out_3));
  // Probe on Result_2_406f29fe
  UCMP ucmp_1 (.in_1(X), .in_2(Y), .out_4(ucmp_1_out_4), .out_3(Equal));
  Multiplexer #(.select(4), .enable("false")) multiplexer_3 (
    .in0(1'b0), .in1(1'b0), .in2(1'b0), .in3(1'b0), .in4(1'b0), .in5(n32bit_adder_1_out_4),
    .in6(sub_1_out_4), .in7(1'b0), .in8(1'b0), .in9(1'b0), .in10(1'b0), .in11(1'b0), .in12(1'b0),
    .in13(1'b0), .in14(1'b0), .in15(1'b0), .out(UnSigned_Overflow_28bd2ab2), .sel(AluOP));
  and and_2 (and_2_out, not_1_out, X[31], Y[31]);
  not not_1 (not_1_out, n32bit_adder_1_out_5[31]);
  or or_2 (or_2_out, and_2_out, and_3_out);
  Multiplexer #(.select(4), .enable("false")) multiplexer_4 (
    .in0(1'b0), .in1(1'b0), .in2(1'b0), .in3(1'b0), .in4(1'b0), .in5(or_2_out), .in6(or_3_out), .in7(1'b0),
    .in8(1'b0), .in9(1'b0), .in10(1'b0), .in11(1'b0), .in12(1'b0), .in13(1'b0), .in14(1'b0), .in15(1'b0),
    .out(Signed_Overflow_350b0444), .sel(AluOP));
  and and_3 (and_3_out, not_2_out, n32bit_adder_1_out_5[31], not_3_out);
  not not_2 (not_2_out, Y[31]);
  not not_3 (not_3_out, X[31]);
  and and_4 (and_4_out, X[31], not_6_out, not_4_out);
  not not_4 (not_4_out, sub_1_out_3[31]);
  or or_3 (or_3_out, and_4_out, and_5_out);
  not not_5 (not_5_out, X[31]);
  not not_6 (not_6_out, Y[31]);
  and and_5 (and_5_out, Y[31], not_5_out, sub_1_out_3[31]);

  // Other names for the same wires on the sheet: OF = Signed_Overflow_350b0444; Result2[31:0] = Result_2_406f29fe;
  //   S[3:0] = AluOP; UOF = UnSigned_Overflow_28bd2ab2

  // Notes on the sheet:
  //   不要改变此引脚区域内容，也不要改变ALU封装形式
  //   输入引脚
  //   请在下方利用上方输入输出引脚的隧道信号构建ALU电路，ctrl+d复制选择部件
  //   华中科技大学计算机学院 计算机组成原理，鸣谢加州大学伯克利CS61C课程
  //   输出引脚
  //   探测区域
endmodule

module L_470d4077 (
  input  [31:0] X,
  input  [31:0] Y,
  input  [3:0] ALUOP,
  output Signed_Overflow_350b0444,
  output Unsigned_overflow_b04ab971,
  output [31:0] Result,
  output [31:0] Result_2_406f29fe,
  output Equal
);

  // Probe on X
  // Probe on X
  ALU alu_1 (
    .AluOP(ALUOP), .X(X), .Equal(Equal), .Result(Result),
    .Signed_Overflow_350b0444(Signed_Overflow_350b0444), .Y(Y), .Result_2_406f29fe(Result_2_406f29fe),
    .UnSigned_Overflow_28bd2ab2(Unsigned_overflow_b04ab971));
  // Probe on ALUOP
  // Probe on Y
  // Probe on Y
  // Probe on Result
  // Probe on Result
  // Probe on Result_2_406f29fe

  // Notes on the sheet:
  //   ALu电路无需调整位置即可连接在该电路中，并且不能出现蓝色线缆和三态输出
endmodule

module L_20504c6a (
  input  [31:0] L_a7ad3258,
  input  [31:0] L_b0369c1b,
  input  L_7b812bbb,
  output [31:0] Result
);

  // Probe on L_a7ad3258
  // Probe on L_a7ad3258
  // Probe on L_b0369c1b
  // Probe on L_b0369c1b
  // Probe on Result
  // Probe on Result

  // Other names for the same wires on the sheet: L_4886a52a[31:0] = Result; L_b298ecfd[31:0] = L_a7ad3258

  // Notes on the sheet:
  //   不要改变此引脚区域内容，也不要改变ALU封装形式
  //   请在下方利用上方输入输出引脚的隧道信号构建等差数列求和电路，ctrl+d复制选择部件
  //   华中科技大学计算机学院 计算机组成原理，鸣谢加州大学伯克利CS61C课程
  //   输出引脚
  //   探测区域
endmodule

module onebit_adder (
  input  A,
  input  B,
  input  Cin,
  output S,
  output Cout
);

  wire and_1_out, and_2_out, and_3_out, xor_1_out;

  and and_1 (and_1_out, A, B);
  and and_2 (and_2_out, A, Cin);
  and and_3 (and_3_out, B, Cin);
  xor xor_1 (xor_1_out, A, B);
  xor xor_2 (S, xor_1_out, Cin);
  or or_1 (Cout, and_1_out, and_2_out, and_3_out);
endmodule

module fourbit_adder (
  input  in_1,
  input  [3:0] in_2,
  input  [3:0] A,
  output [3:0] out_4
);

  wire onebit_adder_1_cout, onebit_adder_2_cout, onebit_adder_3_cout, onebit_adder_4_cout;

  onebit_adder onebit_adder_1 (
    .Cout(onebit_adder_1_cout), .A(A[3]), .Cin(onebit_adder_2_cout), .B(in_2[3]), .S(out_4[3]));
  onebit_adder onebit_adder_2 (
    .Cout(onebit_adder_2_cout), .A(A[2]), .Cin(onebit_adder_3_cout), .B(in_2[2]), .S(out_4[2]));
  onebit_adder onebit_adder_3 (
    .Cout(onebit_adder_3_cout), .A(A[1]), .Cin(onebit_adder_4_cout), .B(in_2[1]), .S(out_4[1]));
  onebit_adder onebit_adder_4 (.Cout(onebit_adder_4_cout), .A(A[0]), .Cin(in_1), .B(in_2[0]), .S(out_4[0]));
endmodule

module fourbit_adder_para (
  input  C0,
  input  [3:0] A,
  input  [3:0] B,
  output [3:0] S,
  output G,
  output Cout,
  output P
);

  wire and_1_out, and_2_out, and_3_out, and_4_out, and_5_out, and_6_out, and_7_out, and_8_out, and_9_out,
       and_10_out, and_11_out, and_12_out, and_13_out, and_14_out, and_15_out, and_16_out, C1, C2, C3,
       onebit_adder_1_cout, or_2_out, or_3_out, or_4_out, or_5_out, or_6_out, or_7_out, or_8_out, or_9_out,
       or_10_out, or_11_out, or_12_out, or_13_out, or_14_out, or_15_out, or_16_out, or_17_out, or_20_out,
       or_21_out, or_22_out, or_23_out;

  or or_1 (Cout, G, and_1_out);
  onebit_adder onebit_adder_1 (.Cout(onebit_adder_1_cout), .A(A[3]), .Cin(C3), .B(B[3]), .S(S[3]));
  or u_G (G, and_5_out, and_2_out, and_3_out, and_4_out);
  and and_1 (and_1_out, C0, P);
  and and_2 (and_2_out, or_2_out, A[2], B[2]);
  and and_3 (and_3_out, A[1], B[1], or_3_out, or_4_out);
  and and_4 (and_4_out, or_5_out, or_6_out, or_7_out, and_6_out);
  and u_P (P, or_8_out, or_9_out, or_10_out, or_11_out);
  and and_5 (and_5_out, A[3], B[3]);
  or or_2 (or_2_out, A[3], B[3]);
  or or_3 (or_3_out, A[2], B[2]);
  or or_4 (or_4_out, A[3], B[3]);
  or or_5 (or_5_out, A[3], B[3]);
  or or_6 (or_6_out, A[2], B[2]);
  or or_7 (or_7_out, A[1], B[1]);
  and and_6 (and_6_out, A[0], B[0]);
  or or_8 (or_8_out, A[3], B[3]);
  or or_9 (or_9_out, A[2], B[2]);
  or or_10 (or_10_out, A[1], B[1]);
  or or_11 (or_11_out, A[0], B[0]);
  onebit_adder onebit_adder_2 (.A(A[2]), .Cin(C2), .B(B[2]), .S(S[2]));  // open: Cout
  or G_2 (C3, and_7_out, and_8_out, and_9_out, and_11_out);
  and and_7 (and_7_out, A[2], B[2]);
  or or_12 (or_12_out, A[2], B[2]);
  and and_8 (and_8_out, or_12_out, A[1], B[1]);
  or or_13 (or_13_out, A[2], B[2]);
  and and_9 (and_9_out, or_13_out, or_14_out, and_10_out);
  or or_14 (or_14_out, A[1], B[1]);
  and and_10 (and_10_out, A[0], B[0]);
  or or_15 (or_15_out, A[2], B[2]);
  and and_11 (and_11_out, or_15_out, or_16_out, or_17_out, C0);
  or or_16 (or_16_out, A[1], B[1]);
  or or_17 (or_17_out, A[0], B[0]);
  onebit_adder onebit_adder_3 (.A(A[1]), .Cin(C1), .B(B[1]), .S(S[1]));  // open: Cout
  or or_18 (C2, and_12_out, and_13_out, and_14_out);
  onebit_adder onebit_adder_4 (.A(A[0]), .Cin(C0), .B(B[0]), .S(S[0]));  // open: Cout
  or or_19 (C1, and_15_out, and_16_out);
  and and_12 (and_12_out, C0, or_20_out, or_21_out);
  and and_13 (and_13_out, A[1], B[1]);
  and and_14 (and_14_out, A[0], B[0], or_22_out);
  and and_15 (and_15_out, A[0], B[0]);
  and and_16 (and_16_out, or_23_out, C0);
  or or_20 (or_20_out, A[0], B[0]);
  or or_21 (or_21_out, A[1], B[1]);
  or or_22 (or_22_out, A[1], B[1]);
  or or_23 (or_23_out, A[0], B[0]);

  // Other names for the same wires on the sheet: C4 = Cout
endmodule

module SN74182 (
  input  Cin,
  input  in_2,
  input  in_3,
  input  in_4,
  input  in_5,
  input  in_6,
  input  in_7,
  input  in_8,
  input  in_9,
  output out_10,
  output Cn_z,
  output Cn_y,
  output Cn_x,
  output out
);

  wire and_1_out, and_2_out, and_3_out, and_4_out, and_5_out, and_6_out, and_7_out, and_8_out, and_9_out,
       and_10_out, and_11_out, and_12_out, and_13_out, Cn, G0, G1, G2, G3, or_1_out, P0, P1, P2, P3;

  and and_1 (and_1_out, G3, G2, G1, G0);
  and and_2 (and_2_out, G3, G2, G1, P1);
  not not_1 (Cn, Cin);
  not not_2 (P0, in_2);
  not not_3 (P1, in_4);
  not not_4 (P2, in_6);
  not not_5 (P3, in_8);
  nor nor_1 (out_10, and_1_out, and_2_out, and_3_out, and_4_out);
  and and_3 (and_3_out, G3, G2, P2);
  not not_6 (G0, in_3);
  not not_7 (G1, in_5);
  not not_8 (G2, in_7);
  not not_9 (G3, in_9);
  and and_4 (and_4_out, P3, G3);
  and and_5 (and_5_out, G2, G1, G0, Cn);
  not not_10 (out, or_1_out);
  nor nor_2 (Cn_z, and_5_out, and_6_out, and_8_out, and_7_out);
  and and_6 (and_6_out, G0, G2, G1, P0);
  or or_1 (or_1_out, P0, P1, P2, P3);
  and and_7 (and_7_out, P2, G2);
  and and_8 (and_8_out, G2, G1, P1);
  and and_9 (and_9_out, G1, G0, Cn);
  nor nor_3 (Cn_y, and_9_out, and_10_out, and_11_out);
  and and_10 (and_10_out, G1, G0, P0);
  and and_11 (and_11_out, P1, G1);
  nor nor_4 (Cn_x, and_12_out, and_13_out);
  and and_12 (and_12_out, P0, G0);
  and and_13 (and_13_out, Cn, G0);

  // Notes on the sheet:
  //   Cn_x: pull=up
endmodule

module _16bit_adder (
  input  [15:0] A,
  input  [15:0] B,
  input  in_3,
  output out_4,
  output out_5,
  output [15:0] out_6
);

  wire fourbit_adder_para_1_g, fourbit_adder_para_1_p, fourbit_adder_para_2_g, fourbit_adder_para_2_p,
       fourbit_adder_para_3_g, fourbit_adder_para_3_p, fourbit_adder_para_4_g, fourbit_adder_para_4_p,
       sn74182_1_cn_x, sn74182_1_cn_y, sn74182_1_cn_z;

  fourbit_adder_para fourbit_adder_para_1 (
    .S(out_6[15:12]), .C0(sn74182_1_cn_z), .A(A[15:12]), .G(fourbit_adder_para_1_g), .B(B[15:12]),
    .P(fourbit_adder_para_1_p));  // open: Cout
  fourbit_adder_para fourbit_adder_para_2 (
    .S(out_6[11:8]), .C0(sn74182_1_cn_y), .A(A[11:8]), .G(fourbit_adder_para_2_g), .B(B[11:8]),
    .P(fourbit_adder_para_2_p));  // open: Cout
  fourbit_adder_para fourbit_adder_para_3 (
    .S(out_6[7:4]), .C0(sn74182_1_cn_x), .A(A[7:4]), .G(fourbit_adder_para_3_g), .B(B[7:4]),
    .P(fourbit_adder_para_3_p));  // open: Cout
  SN74182 sn74182_1 (
    .Cin(in_3), .out(out_5), .out_10(out_4), .Cn_y(sn74182_1_cn_y), .Cn_x(sn74182_1_cn_x),
    .in_2(fourbit_adder_para_4_p), .in_3(fourbit_adder_para_4_g), .in_4(fourbit_adder_para_3_p),
    .in_5(fourbit_adder_para_3_g), .in_6(fourbit_adder_para_2_p), .in_7(fourbit_adder_para_2_g),
    .in_8(fourbit_adder_para_1_p), .in_9(fourbit_adder_para_1_g), .Cn_z(sn74182_1_cn_z));
  fourbit_adder_para fourbit_adder_para_4 (
    .S(out_6[3:0]), .C0(in_3), .A(A[3:0]), .G(fourbit_adder_para_4_g), .B(B[3:0]), .P(fourbit_adder_para_4_p));  // open: Cout

  // Other names for the same wires on the sheet: A0[3:0] = A[3:0]; A1[3:0] = A[7:4]; A2[3:0] = A[11:8];
  //   A3[3:0] = A[15:12]; B0[3:0] = B[3:0]; B1[3:0] = B[7:4]; B2[3:0] = B[11:8]; B3[3:0] = B[15:12]; Cn = in_3
endmodule

module _32bit_adder (
  input  in_1,
  input  [31:0] A,
  input  [31:0] B,
  output out_4,
  output [31:0] out_5
);

  wire n16bit_adder_1_out_4, n16bit_adder_1_out_5, n16bit_adder_2_out_4, n16bit_adder_2_out_5, sn74182_1_cn_x;

  _16bit_adder u_16bit_adder_1 (
    .out_4(n16bit_adder_1_out_4), .out_5(n16bit_adder_1_out_5), .out_6(out_5[31:16]), .A(A[31:16]),
    .B(B[31:16]), .in_3(sn74182_1_cn_x));
  _16bit_adder u_16bit_adder_2 (
    .out_4(n16bit_adder_2_out_4), .out_5(n16bit_adder_2_out_5), .out_6(out_5[15:0]), .A(A[15:0]),
    .B(B[15:0]), .in_3(in_1));
  SN74182 sn74182_1 (
    .Cin(in_1), .Cn_y(out_4), .Cn_x(sn74182_1_cn_x), .in_2(n16bit_adder_2_out_5),
    .in_3(n16bit_adder_2_out_4), .in_4(n16bit_adder_1_out_5), .in_5(n16bit_adder_1_out_4));  // open: out, out_10, in_6, in_7, in_8, in_9, Cn_z

  // Other names for the same wires on the sheet: A0[15:0] = A[15:0]; A1[15:0] = A[31:16]; B0[15:0] = B[15:0];
  //   B1[15:0] = B[31:16]
endmodule

module functions (
  input  [3:0] in_1,
  input  [31:0] in_2,
  input  [31:0] in_3
);

  wire [3:0] multiplexer_1_out, undriven, undriven_2, undriven_3, undriven_4, undriven_5, undriven_6,
       undriven_7, undriven_8, undriven_9, undriven_10, undriven_11, undriven_12, undriven_13, undriven_14,
       undriven_15, undriven_16;
  wire [31:0] shifter_1_out, shifter_2_out, shifter_3_out;

  Multiplexer #(.select(4), .width(4), .enable("false")) multiplexer_1 (
    .in0(undriven), .in1(undriven_2), .in2(undriven_3), .in3(undriven_4), .in4(undriven_5), .in5(undriven_6),
    .in6(undriven_7), .in7(undriven_8), .in8(undriven_9), .in9(undriven_10), .in10(undriven_11),
    .in11(undriven_12), .in12(undriven_13), .in13(undriven_14), .in14(undriven_15), .in15(undriven_16),
    .out(multiplexer_1_out), .sel(in_1));
  Shifter #(.width(32)) shifter_1 (.in(in_2), .\dist (in_3[4:0]), .out(shifter_1_out));
  Shifter #(.width(32), .shift("lr")) shifter_2 (.in(in_2), .\dist (in_3[4:0]), .out(shifter_2_out));
  Shifter #(.width(32), .shift("ar")) shifter_3 (.in(in_2), .\dist (in_3[4:0]), .out(shifter_3_out));
  _32bit_adder u_32bit_adder ();  // open: A, B, in_1, out_5, out_4
  Comparator #(.width(32)) comparator_1 (.a(in_2), .b(in_3));  // open: gt, eq, lt
  Multiplier #(.width(32)) multiplier_1 (.a(in_2), .b(in_3));  // open: out, cin, cout
  Divider #(.width(32)) divider_1 (.a(in_2), .b(in_3));  // open: out, upper, rem
  // OR_Gate OR has open pins: in0=in_2, in1=in_3, out=open
  _32bit_adder u_32bit_adder_2 ();  // open: A, B, in_1, out_5, out_4
  // XOR_Gate XOR has open pins: in0=in_2, in1=in_3, out=open
  // NOR_Gate NOR has open pins: in0=in_2, in1=in_3, out=open

  // Other names for the same wires on the sheet: A[31:0] = in_2; ALU_OP[3:0] = in_1; B[31:0] = in_3

  // Notes on the sheet:
  //   32bit-adder 
  //   substractor
endmodule

module AND (
  input  [31:0] in_1,
  input  [31:0] in_2,
  output [31:0] out_3
);

  assign out_3 = in_1 & in_2;  // AND_Gate AND, 32 bits wide

  // Other names for the same wires on the sheet: X[31:0] = in_1; Y[31:0] = in_2
endmodule

module OR (
  input  [31:0] in_1,
  input  [31:0] in_2,
  output [31:0] out_3
);

  assign out_3 = in_1 | in_2;  // OR_Gate OR, 32 bits wide

  // Other names for the same wires on the sheet: X[31:0] = in_1; Y[31:0] = in_2
endmodule

module SHL (
  input  [31:0] in_1,
  input  [31:0] in_2,
  output [31:0] out_3
);

  Shifter #(.width(32)) shifter_1 (.in(in_1), .\dist (in_2[4:0]), .out(out_3));

  // Other names for the same wires on the sheet: X[31:0] = in_1; Y[31:0] = in_2
endmodule

module SHR (
  input  [31:0] in_1,
  input  [31:0] in_2,
  output [31:0] out_3
);

  Shifter #(.width(32), .shift("lr")) shifter_1 (.in(in_1), .\dist (in_2[4:0]), .out(out_3));

  // Other names for the same wires on the sheet: X[31:0] = in_1; Y[31:0] = in_2
endmodule

module SAR (
  input  [31:0] in_1,
  input  [31:0] in_2,
  output [31:0] out_3
);

  Shifter #(.width(32), .shift("ar")) shifter_1 (.in(in_1), .\dist (in_2[4:0]), .out(out_3));

  // Other names for the same wires on the sheet: X[31:0] = in_1; Y[31:0] = in_2
endmodule

module XOR (
  input  [31:0] in_1,
  input  [31:0] in_2,
  output [31:0] out_3
);

  assign out_3 = in_1 ^ in_2;  // XOR_Gate XOR, 32 bits wide

  // Other names for the same wires on the sheet: X[31:0] = in_1; Y[31:0] = in_2
endmodule

module NOR (
  input  [31:0] in_1,
  input  [31:0] in_2,
  output [31:0] out_3
);

  assign out_3 = ~(in_1 | in_2);  // NOR_Gate NOR, 32 bits wide

  // Other names for the same wires on the sheet: X[31:0] = in_1; Y[31:0] = in_2
endmodule

module SCMP (
  input  [31:0] in_1,
  input  [31:0] in_2,
  output [31:0] out_3
);

  Comparator #(.width(32)) comparator_1 (.a(in_1), .b(in_2), .lt(out_3[0]));  // open: gt, eq

  assign out_3[31:1] = {31{1'b0}};

  // Other names for the same wires on the sheet: X[31:0] = in_1; Y[31:0] = in_2
endmodule

module UCMP (
  input  [31:0] in_1,
  input  [31:0] in_2,
  output out_3,
  output [31:0] out_4
);

  Comparator #(.width(32), .mode("unsigned")) comparator_1 (.a(in_1), .b(in_2), .eq(out_3), .lt(out_4[0]));  // open: gt

  assign out_4[31:1] = {31{1'b0}};

  // Other names for the same wires on the sheet: X[31:0] = in_1; Y[31:0] = in_2
endmodule

module MUL (
  input  [31:0] in_1,
  input  [31:0] in_2,
  output [31:0] out_3,
  output [31:0] out_4
);

  Multiplier #(.width(32)) multiplier_1 (.a(in_1), .b(in_2), .out(out_3), .cout(out_4));  // open: cin

  // Other names for the same wires on the sheet: X[31:0] = in_1; Y[31:0] = in_2
endmodule

module DIV (
  input  [31:0] in_1,
  input  [31:0] in_2,
  output [31:0] out_3,
  output [31:0] out_4
);

  Divider #(.width(32)) divider_1 (.a(in_1), .b(in_2), .out(out_3), .rem(out_4));  // open: upper

  // Other names for the same wires on the sheet: X[31:0] = in_1; Y[31:0] = in_2
endmodule

module SUB (
  input  [31:0] X,
  input  [31:0] Y,
  output [31:0] out_3,
  output out_4
);

  wire n32bit_adder_1_out_4;
  wire [31:0] not_1_out, not_3_out, xor_1_out;

  assign not_1_out = ~xor_1_out;  // NOT_Gate not_1, 32 bits wide
  assign xor_1_out = X ^ X;  // XOR_Gate xor_1, 32 bits wide
  not not_2 (out_4, n32bit_adder_1_out_4);
  _32bit_adder u_32bit_adder_1 (
    .A(X), .B(not_3_out), .in_1(not_1_out[31]), .out_5(out_3), .out_4(n32bit_adder_1_out_4));
  assign not_3_out = ~Y;  // NOT_Gate not_3, 32 bits wide
endmodule
