// Logisim project Control.circ as structural Verilog: 23 circuits, main circuit main
module main (
  input  [1:0] INT_SRC,
  input  [2:0] oldIR,
  input  Greater0,
  input  [5:0] op,
  input  [5:0] funct,
  input  in_6,
  output Finish,
  output [2:0] newIR,
  output IE,
  output [2:0] Clear,
  output [3:0] AluControl,
  output Extype,
  output RegDst,
  output AluShift,
  output R1Src,
  output RegWrite,
  output Jump,
  output PCToReg,
  output Branch,
  output W31,
  output SysCall,
  output AluSrc,
  output JmpReg,
  output MemWrite,
  output MemRead,
  output MemToReg,
  output SelectBase
);

  wire Add, add_t, addi, addiu, addu, And, and_1_out, and_t, andi, beq, bgtz, bne, IC1_beq, IC1_bne, j, jal,
       jr, lw, MFC0, \new , Nor, Or, or_6_out, or_7_out, or_8_out, or_12_out, or_t, ori, RegWrite1_regwrite1,
       RegWrite2_regwrite2, SLL, SLT, slt_t, slti, sltiu, SLTU, SRA, SRL, Sub, sw, syscall_t, xori;
  wire [2:0] demultiplexer_1_out1;

  and and_1 (and_1_out, bgtz, 1'b1);
  IC0 IC0 (
    .op0(op[5]), .op1(op[4]), .op2(op[3]), .op3(op[2]), .op4(op[1]), .op5(op[0]), .funct0(funct[5]),
    .funct1(funct[4]), .funct2(funct[3]), .funct3(funct[2]), .funct4(funct[1]), .funct5(funct[0]),
    .add(add_t), .addi(addi), .addiu(addiu), .addu(addu), .\and (and_t), .andi(andi), .sll(SLL), .sra(SRA),
    .srl(SRL), .sub(Sub), .\or (or_t), .ori(ori));
  or or_1 (Add, add_t, addi, addiu, addu, lw, sw);
  or or_2 (And, and_t, andi);
  or or_3 (Or, or_t, ori);
  or or_4 (SLT, slt_t, slti);
  Jump jump_1 (.j(j), .jal(jal), .jr(jr), .Jump(Jump));
  Branch branch_1 (.beq(and_1_out), .bne(beq), .\new (bne), .Branch(Branch));
  SysCall syscall_1 (.syscall(syscall_t), .SysCall_2(SysCall));
  JmpReg jmpreg_1 (.jr(jr), .JmpReg(JmpReg));
  IC3 ic3_1 (
    .op0(op[5]), .op1(op[4]), .op2(op[3]), .op3(op[2]), .op4(op[1]), .op5(op[0]), .funct0(funct[5]),
    .funct1(funct[4]), .funct2(funct[3]), .funct3(funct[2]), .funct4(funct[1]), .funct5(funct[0]),
    .MFC0(MFC0), .ERET(Finish));
  or or_5 (Extype, andi, sltiu, xori, ori);
  RegDst u_RegDst (
    .add(add_t), .addu(addu), .\and (and_t), .sll(SLL), .sra(SRA), .srl(SRL), .sub(Sub), .\or (or_t),
    .\nor (Nor), .slt(slt_t), .RegDst(RegDst));
  AluShift alushift_1 (.sll(SLL), .sra(SRA), .srl(SRL), .AluShift(AluShift));
  RegWrite1 RegWrite1 (
    .add(add_t), .addi(addi), .addiu(addiu), .addu(addu), .\and (and_t), .andi(andi), .sll(SLL), .sra(SRA),
    .srl(SRL), .sub(Sub), .\or (or_t), .ori(ori), .RegWrite1(RegWrite1_regwrite1));
  RegWrite2 RegWrite2 (
    .\nor (sltiu), .lw(xori), .slt(Nor), .slti(lw), .sltu(slt_t), .jal(slti), .xori(SLTU), .sltiu(jal),
    .RegWrite2(RegWrite2_regwrite2));
  AluSrc alusrc_1 (
    .addi(addi), .addiu(addiu), .andi(andi), .ori(ori), .lw(lw), .sw(sw), .slti(slti), .\new (\new ),
    .AluSrc(AluSrc));
  MemWrite memwrite_1 (.sw(sw), .sh(SelectBase), .MemWrite(MemWrite));
  MemRead memread_1 (.lw(lw), .MemRead(MemRead));
  MemToReg memtoreg_1 (.lw(lw), .MemToReg(MemToReg));
  PCToReg pctoreg_1 (.jal(jal), .PCToReg(PCToReg));
  Demultiplexer #(.select(2), .enable("false")) demultiplexer_1 (
    .out1(demultiplexer_1_out1[0]), .out2(demultiplexer_1_out1[1]), .out3(demultiplexer_1_out1[2]),
    .in(MFC0), .sel(INT_SRC));  // open: out0
  or or_6 (or_6_out, sltiu, bgtz, xori);
  or or_7 (or_7_out, sltiu, SelectBase);
  or or_8 (or_8_out, bgtz, xori, SelectBase);
  or or_9 (RegWrite, RegWrite1_regwrite1, RegWrite2_regwrite2);
  or or_10 (AluControl[3], Or, Nor, or_6_out, SLTU, SLT);
  or or_11 (AluControl[2], Add, Sub, or_7_out, And, SLTU);
  or or_12 (or_12_out, SRL, Sub, And, Nor, SLT);
  or or_13 (AluControl[0], SRA, Add, or_8_out, And, SLT);
  or or_14 (AluControl[1], bgtz, or_12_out);
  IR ir_1 (.oldIR(oldIR), .INT_SRC(INT_SRC), .in_2({Finish, MFC0}), .out_4(Clear));
  IC2 ic2_1 (
    .op0(op[5]), .op1(op[4]), .op2(op[3]), .op3(op[2]), .op4(op[1]), .op5(op[0]), .xori(xori), .sltiu(sltiu),
    .sh(SelectBase), .bgtz(bgtz));
  or or_15 (\new , SelectBase, sltiu, xori);
  IC1 IC1 (
    .op0(op[5]), .op1(op[4]), .op2(op[3]), .op3(op[2]), .op4(op[1]), .op5(op[0]), .funct0(funct[5]),
    .funct1(funct[4]), .funct2(funct[3]), .funct3(funct[2]), .funct4(funct[1]), .funct5(funct[0]),
    .\nor (Nor), .lw(lw), .sw(sw), .beq(IC1_beq), .bne(IC1_bne), .slt(slt_t), .slti(slti), .sltu(SLTU),
    .j(j), .jal(jal), .jr(jr), .syscall(syscall_t));
  and and_2 (beq, IC1_beq, 1'b1);
  and and_3 (bne, IC1_bne, ~1'b0);  // AND_Gate

  assign IE = 1'b1;
  assign newIR = Clear;
  assign R1Src = AluShift;
  assign W31 = PCToReg;

  // Other names for the same wires on the sheet: ERET = Finish; Equal = in_6; sh = SelectBase
endmodule

module IC0 (
  input  op0,
  input  op1,
  input  op2,
  input  op3,
  input  op4,
  input  op5,
  input  funct0,
  input  funct1,
  input  funct2,
  input  funct3,
  input  funct4,
  input  funct5,
  output add,
  output addi,
  output addiu,
  output addu,
  output \and ,
  output andi,
  output sll,
  output sra,
  output srl,
  output sub,
  output \or ,
  output ori
);

  wire not_1_out, not_2_out, not_3_out, not_4_out, not_5_out, not_6_out, not_7_out, not_8_out, not_9_out,
       not_10_out, not_11_out, not_12_out, not_13_out, not_14_out, not_15_out, not_16_out, not_17_out,
       not_18_out, not_19_out, not_20_out, not_21_out, not_22_out, not_23_out, not_24_out, not_25_out,
       not_26_out, not_27_out, not_28_out, not_29_out, not_30_out, not_31_out, not_32_out, not_33_out,
       not_34_out, not_35_out, not_36_out, not_37_out, not_38_out, not_39_out, not_40_out, not_41_out,
       not_42_out, not_43_out, not_44_out, not_45_out, not_46_out, not_47_out, not_48_out, not_49_out,
       not_50_out, not_51_out, not_52_out, not_53_out, not_54_out, not_55_out, not_56_out, not_57_out,
       not_58_out, not_59_out, not_60_out, not_61_out, not_62_out, not_63_out, not_64_out, not_65_out,
       not_66_out, not_67_out, not_68_out, not_69_out, not_70_out, not_71_out, not_72_out, not_73_out,
       not_74_out, not_75_out, not_76_out, not_77_out, not_78_out, not_79_out, not_80_out, not_81_out,
       not_82_out, not_83_out, not_84_out, not_85_out, not_86_out, not_87_out, not_88_out, not_89_out,
       not_90_out, not_91_out, not_92_out, not_93_out, not_94_out, not_95_out, not_96_out, not_97_out,
       not_98_out, not_99_out;

  not not_1 (not_1_out, op0);
  not not_2 (not_2_out, op1);
  not not_3 (not_3_out, op2);
  not not_4 (not_4_out, op3);
  not not_5 (not_5_out, op4);
  not not_6 (not_6_out, op5);
  not not_7 (not_7_out, funct1);
  not not_8 (not_8_out, funct2);
  not not_9 (not_9_out, funct3);
  not not_10 (not_10_out, funct4);
  not not_11 (not_11_out, funct5);
  not not_12 (not_12_out, op0);
  not not_13 (not_13_out, op1);
  not not_14 (not_14_out, op3);
  not not_15 (not_15_out, op4);
  not not_16 (not_16_out, op5);
  not not_17 (not_17_out, op0);
  not not_18 (not_18_out, op1);
  not not_19 (not_19_out, op3);
  not not_20 (not_20_out, op4);
  not not_21 (not_21_out, op0);
  not not_22 (not_22_out, op1);
  not not_23 (not_23_out, op2);
  not not_24 (not_24_out, op3);
  not not_25 (not_25_out, op4);
  not not_26 (not_26_out, op5);
  not not_27 (not_27_out, funct1);
  not not_28 (not_28_out, funct2);
  not not_29 (not_29_out, funct3);
  not not_30 (not_30_out, funct4);
  not not_31 (not_31_out, op0);
  not not_32 (not_32_out, op1);
  not not_33 (not_33_out, op2);
  not not_34 (not_34_out, op3);
  not not_35 (not_35_out, op4);
  not not_36 (not_36_out, op5);
  not not_37 (not_37_out, funct1);
  not not_38 (not_38_out, funct2);
  not not_39 (not_39_out, funct4);
  not not_40 (not_40_out, funct5);
  not not_41 (not_41_out, op0);
  not not_42 (not_42_out, op1);
  not not_43 (not_43_out, op4);
  not not_44 (not_44_out, op5);
  not not_45 (not_45_out, op0);
  not not_46 (not_46_out, op1);
  not not_47 (not_47_out, op2);
  not not_48 (not_48_out, op3);
  not not_49 (not_49_out, op4);
  not not_50 (not_50_out, op5);
  not not_51 (not_51_out, funct0);
  not not_52 (not_52_out, funct1);
  not not_53 (not_53_out, funct2);
  not not_54 (not_54_out, funct3);
  not not_55 (not_55_out, funct4);
  not not_56 (not_56_out, funct5);
  not not_57 (not_57_out, op0);
  not not_58 (not_58_out, op1);
  not not_59 (not_59_out, op2);
  not not_60 (not_60_out, op3);
  not not_61 (not_61_out, op4);
  not not_62 (not_62_out, op5);
  not not_63 (not_63_out, funct0);
  not not_64 (not_64_out, funct1);
  not not_65 (not_65_out, funct2);
  not not_66 (not_66_out, funct3);
  not not_67 (not_67_out, op0);
  not not_68 (not_68_out, op1);
  not not_69 (not_69_out, op2);
  not not_70 (not_70_out, op3);
  not not_71 (not_71_out, op4);
  not not_72 (not_72_out, op5);
  not not_73 (not_73_out, funct0);
  not not_74 (not_74_out, funct1);
  not not_75 (not_75_out, funct2);
  not not_76 (not_76_out, funct3);
  not not_77 (not_77_out, funct5);
  not not_78 (not_78_out, op0);
  not not_79 (not_79_out, op1);
  not not_80 (not_80_out, op2);
  not not_81 (not_81_out, op3);
  not not_82 (not_82_out, op4);
  not not_83 (not_83_out, op5);
  not not_84 (not_84_out, funct1);
  not not_85 (not_85_out, funct2);
  not not_86 (not_86_out, funct3);
  not not_87 (not_87_out, funct5);
  not not_88 (not_88_out, op0);
  not not_89 (not_89_out, op1);
  not not_90 (not_90_out, op2);
  not not_91 (not_91_out, op3);
  not not_92 (not_92_out, op4);
  not not_93 (not_93_out, op5);
  not not_94 (not_94_out, funct1);
  not not_95 (not_95_out, funct2);
  not not_96 (not_96_out, funct4);
  not not_97 (not_97_out, op0);
  not not_98 (not_98_out, op1);
  not not_99 (not_99_out, op4);
  and and_1 (add, not_1_out, not_2_out, not_3_out, not_4_out, not_5_out, not_6_out, funct0, not_7_out, not_8_out, not_9_out, not_10_out, not_11_out);
  and and_2 (addi, not_12_out, not_13_out, op2, not_14_out, not_15_out, not_16_out);
  and and_3 (addiu, not_17_out, not_18_out, op2, not_19_out, not_20_out, op5);
  and and_4 (addu, not_21_out, not_22_out, not_23_out, not_24_out, not_25_out, not_26_out, funct0, not_27_out, not_28_out, not_29_out, not_30_out, funct5);
  and and_5 (\and , not_31_out, not_32_out, not_33_out, not_34_out, not_35_out, not_36_out, funct0, not_37_out, not_38_out, funct3, not_39_out, not_40_out);
  and and_6 (andi, not_41_out, not_42_out, op2, op3, not_43_out, not_44_out);
  and and_7 (sll, not_45_out, not_46_out, not_47_out, not_48_out, not_49_out, not_50_out, not_51_out, not_52_out, not_53_out, not_54_out, not_55_out, not_56_out);
  and and_8 (sra, not_57_out, not_58_out, not_59_out, not_60_out, not_61_out, not_62_out, not_63_out, not_64_out, not_65_out, not_66_out, funct4, funct5);
  and and_9 (srl, not_67_out, not_68_out, not_69_out, not_70_out, not_71_out, not_72_out, not_73_out, not_74_out, not_75_out, not_76_out, funct4, not_77_out);
  and and_10 (sub, not_78_out, not_79_out, not_80_out, not_81_out, not_82_out, not_83_out, funct0, not_84_out, not_85_out, not_86_out, funct4, not_87_out);
  and and_11 (\or , not_88_out, not_89_out, not_90_out, not_91_out, not_92_out, not_93_out, funct0, not_94_out, not_95_out, funct3, not_96_out, funct5);
  and and_12 (ori, not_97_out, not_98_out, op2, op3, not_99_out, op5);
endmodule

module IC1 (
  input  op0,
  input  op1,
  input  op2,
  input  op3,
  input  op4,
  input  op5,
  input  funct0,
  input  funct1,
  input  funct2,
  input  funct3,
  input  funct4,
  input  funct5,
  output \nor ,
  output lw,
  output sw,
  output beq,
  output bne,
  output slt,
  output slti,
  output sltu,
  output j,
  output jal,
  output jr,
  output syscall
);

  wire not_1_out, not_2_out, not_3_out, not_4_out, not_5_out, not_6_out, not_7_out, not_8_out, not_9_out,
       not_10_out, not_11_out, not_12_out, not_13_out, not_14_out, not_15_out, not_16_out, not_17_out,
       not_18_out, not_19_out, not_20_out, not_21_out, not_22_out, not_23_out, not_24_out, not_25_out,
       not_26_out, not_27_out, not_28_out, not_29_out, not_30_out, not_31_out, not_32_out, not_33_out,
       not_34_out, not_35_out, not_36_out, not_37_out, not_38_out, not_39_out, not_40_out, not_41_out,
       not_42_out, not_43_out, not_44_out, not_45_out, not_46_out, not_47_out, not_48_out, not_49_out,
       not_50_out, not_51_out, not_52_out, not_53_out, not_54_out, not_55_out, not_56_out, not_57_out,
       not_58_out, not_59_out, not_60_out, not_61_out, not_62_out, not_63_out, not_64_out, not_65_out,
       not_66_out, not_67_out, not_68_out, not_69_out, not_70_out, not_71_out, not_72_out, not_73_out;

  not not_1 (not_1_out, op0);
  not not_2 (not_2_out, op1);
  not not_3 (not_3_out, op2);
  not not_4 (not_4_out, op3);
  not not_5 (not_5_out, op4);
  not not_6 (not_6_out, op5);
  not not_7 (not_7_out, funct1);
  not not_8 (not_8_out, funct2);
  not not_9 (not_9_out, op1);
  not not_10 (not_10_out, op2);
  not not_11 (not_11_out, op3);
  not not_12 (not_12_out, op1);
  not not_13 (not_13_out, op3);
  not not_14 (not_14_out, op0);
  not not_15 (not_15_out, op1);
  not not_16 (not_16_out, op2);
  not not_17 (not_17_out, op4);
  not not_18 (not_18_out, op5);
  not not_19 (not_19_out, op0);
  not not_20 (not_20_out, op1);
  not not_21 (not_21_out, op2);
  not not_22 (not_22_out, op4);
  not not_23 (not_23_out, op0);
  not not_24 (not_24_out, op1);
  not not_25 (not_25_out, op2);
  not not_26 (not_26_out, op3);
  not not_27 (not_27_out, op4);
  not not_28 (not_28_out, op5);
  not not_29 (not_29_out, funct1);
  not not_30 (not_30_out, funct3);
  not not_31 (not_31_out, funct5);
  not not_32 (not_32_out, op0);
  not not_33 (not_33_out, op1);
  not not_34 (not_34_out, op3);
  not not_35 (not_35_out, op5);
  not not_36 (not_36_out, op0);
  not not_37 (not_37_out, op1);
  not not_38 (not_38_out, op2);
  not not_39 (not_39_out, op3);
  not not_40 (not_40_out, op4);
  not not_41 (not_41_out, op5);
  not not_42 (not_42_out, funct1);
  not not_43 (not_43_out, funct3);
  not not_44 (not_44_out, op0);
  not not_45 (not_45_out, op1);
  not not_46 (not_46_out, op2);
  not not_47 (not_47_out, op3);
  not not_48 (not_48_out, op5);
  not not_49 (not_49_out, op0);
  not not_50 (not_50_out, op1);
  not not_51 (not_51_out, op2);
  not not_52 (not_52_out, op3);
  not not_53 (not_53_out, op0);
  not not_54 (not_54_out, op1);
  not not_55 (not_55_out, op2);
  not not_56 (not_56_out, op3);
  not not_57 (not_57_out, op4);
  not not_58 (not_58_out, op5);
  not not_59 (not_59_out, funct0);
  not not_60 (not_60_out, funct1);
  not not_61 (not_61_out, funct3);
  not not_62 (not_62_out, funct4);
  not not_63 (not_63_out, funct5);
  not not_64 (not_64_out, op0);
  not not_65 (not_65_out, op1);
  not not_66 (not_66_out, op2);
  not not_67 (not_67_out, op3);
  not not_68 (not_68_out, op4);
  not not_69 (not_69_out, op5);
  not not_70 (not_70_out, funct0);
  not not_71 (not_71_out, funct1);
  not not_72 (not_72_out, funct4);
  not not_73 (not_73_out, funct5);
  and and_1 (\nor , not_1_out, not_2_out, not_3_out, not_4_out, not_5_out, not_6_out, funct0, not_7_out, not_8_out, funct3, funct4, funct5);
  and and_2 (lw, op0, not_9_out, not_10_out, not_11_out, op4, op5);
  and and_3 (sw, op0, not_12_out, op2, not_13_out, op4, op5);
  and and_4 (beq, not_14_out, not_15_out, not_16_out, op3, not_17_out, not_18_out);
  and and_5 (bne, not_19_out, not_20_out, not_21_out, op3, not_22_out, op5);
  and and_6 (slt, not_23_out, not_24_out, not_25_out, not_26_out, not_27_out, not_28_out, funct0, not_29_out, funct2, not_30_out, funct4, not_31_out);
  and and_7 (slti, not_32_out, not_33_out, op2, not_34_out, op4, not_35_out);
  and and_8 (sltu, not_36_out, not_37_out, not_38_out, not_39_out, not_40_out, not_41_out, funct0, not_42_out, funct2, not_43_out, funct4, funct5);
  and and_9 (j, not_44_out, not_45_out, not_46_out, not_47_out, op4, not_48_out);
  and and_10 (jal, not_49_out, not_50_out, not_51_out, not_52_out, op4, op5);
  and and_11 (jr, not_53_out, not_54_out, not_55_out, not_56_out, not_57_out, not_58_out, not_59_out, not_60_out, funct2, not_61_out, not_62_out, not_63_out);
  and and_12 (syscall, not_64_out, not_65_out, not_66_out, not_67_out, not_68_out, not_69_out, not_70_out, not_71_out, funct2, funct3, not_72_out, not_73_out);
endmodule

module RegDst (
  input  add,
  input  addu,
  input  \and ,
  input  sll,
  input  sra,
  input  srl,
  input  sub,
  input  \or ,
  input  \nor ,
  input  slt,
  output RegDst
);

  or or_1 (RegDst, add, addu, \and , sll, sra, srl, sub, \or , \nor , slt);
endmodule

module RegWrite1 (
  input  add,
  input  addi,
  input  addiu,
  input  addu,
  input  \and ,
  input  andi,
  input  sll,
  input  sra,
  input  srl,
  input  sub,
  input  \or ,
  input  ori,
  output RegWrite1
);

  or or_1 (RegWrite1, add, addi, addiu, addu, \and , andi, sll, sra, srl, sub, \or , ori);
endmodule

module RegWrite2 (
  input  \nor ,
  input  lw,
  input  slt,
  input  slti,
  input  sltu,
  input  jal,
  input  xori,
  input  sltiu,
  output RegWrite2
);

  or or_1 (RegWrite2, \nor , lw, slt, slti, sltu, jal, sltiu, xori);
endmodule

module AluSrc (
  input  addi,
  input  addiu,
  input  andi,
  input  ori,
  input  lw,
  input  sw,
  input  slti,
  input  \new ,
  output AluSrc
);

  or or_1 (AluSrc, addi, addiu, andi, ori, lw, sw, slti, \new );
endmodule

module MemWrite (
  input  sw,
  input  sh,
  output MemWrite
);

  or or_1 (MemWrite, sw, sh);
endmodule

module MemRead (
  input  lw,
  output MemRead
);

  buf or_1 (MemRead, lw);  // OR_Gate
endmodule

module MemToReg (
  input  lw,
  output MemToReg
);

  buf or_1 (MemToReg, lw);  // OR_Gate
endmodule

module Branch (
  input  beq,
  input  bne,
  input  \new ,
  output Branch
);

  or or_1 (Branch, beq, bne, \new );
endmodule

module Jump (
  input  j,
  input  jal,
  input  jr,
  output Jump
);

  or or_1 (Jump, j, jal, jr);
endmodule

module SysCall (
  input  syscall,
  output SysCall_2
);


  assign SysCall_2 = syscall;
endmodule

module ALU_op (
  input  add,
  input  OP0,
  input  addi,
  input  OP1,
  input  addiu,
  input  OP2,
  input  addu,
  input  OP3,
  input  lw,
  input  sw,
  input  sub,
  input  \and ,
  input  andi,
  input  \or ,
  input  ori,
  input  \nor ,
  input  sll,
  input  srl,
  input  sra,
  input  sltu,
  input  slt,
  input  slti,
  output SLL_2
);

  wire Add_t, And_t, not_1_out, not_2_out, not_3_out, not_4_out, not_5_out, not_6_out, not_7_out, not_8_out,
       not_9_out, not_10_out, not_11_out, not_12_out, not_13_out, not_14_out, not_15_out, not_16_out,
       not_17_out, not_18_out, not_19_out, not_20_out, not_21_out, not_22_out, not_23_out, Or_t, SLT_t;

  or or_1 (Add_t, add, addi, addiu, addu, lw, sw);
  or or_2 (And_t, \and , andi);
  or or_3 (Or_t, \or , ori);
  or or_4 (SLT_t, slt, slti);
  not not_1 (not_1_out, OP0);
  not not_2 (not_2_out, OP2);
  not not_3 (not_3_out, OP0);
  not not_4 (not_4_out, OP3);
  not not_5 (not_5_out, OP0);
  not not_6 (not_6_out, OP1);
  not not_7 (not_7_out, OP2);
  not not_8 (not_8_out, OP3);
  not not_9 (not_9_out, OP1);
  not not_10 (not_10_out, OP3);
  not not_11 (not_11_out, OP0);
  not not_12 (not_12_out, OP1);
  not not_13 (not_13_out, OP2);
  not not_14 (not_14_out, OP3);
  not not_15 (not_15_out, OP0);
  not not_16 (not_16_out, OP1);
  not not_17 (not_17_out, OP3);
  not not_18 (not_18_out, OP0);
  not not_19 (not_19_out, OP1);
  not not_20 (not_20_out, OP2);
  not not_21 (not_21_out, OP2);
  not not_22 (not_22_out, OP3);
  not not_23 (not_23_out, OP1);
  and and_1 (Add_t, not_1_out, OP1, not_2_out, OP3);
  and and_2 (sub, not_3_out, OP1, OP2, not_4_out);
  and and_3 (And_t, not_5_out, OP1, OP2, OP3);
  and and_4 (Or_t, OP0, not_6_out, not_7_out, not_8_out);
  and and_5 (\nor , OP0, not_9_out, OP2, not_10_out);
  and and_6 (SLL_2, not_11_out, not_12_out, not_13_out, not_14_out);
  and and_7 (srl, not_15_out, not_16_out, OP2, not_17_out);
  and and_8 (sra, not_18_out, not_19_out, not_20_out, OP3);
  and and_9 (sltu, OP0, OP1, not_21_out, not_22_out);
  and and_10 (SLT_t, OP0, not_23_out, OP2, OP3);
endmodule

module AluShift (
  input  sll,
  input  sra,
  input  srl,
  output AluShift
);

  or or_1 (AluShift, sll, sra, srl);
endmodule

module PCToReg (
  input  jal,
  output PCToReg
);


  assign PCToReg = jal;
endmodule

module R1Src (
  input  sll,
  input  sra,
  input  srl,
  output R1Src
);

  or or_1 (R1Src, sll, sra, srl);
endmodule

module JmpReg (
  input  jr,
  output JmpReg
);


  assign JmpReg = jr;
endmodule

module W31 (
  input  jal,
  output W31
);


  assign W31 = jal;
endmodule

module ALU_OP (
  input  Add,
  input  Sub,
  input  And,
  input  Or,
  input  Nor,
  input  SLL,
  input  SRL,
  input  SRA,
  input  SLTU,
  input  SLT,
  output OP0,
  output OP1,
  output OP2,
  output OP3
);

  or or_1 (OP0, Or, Nor, SLTU, SLT);
  or or_2 (OP1, Add, Sub, And, SLTU);
  or or_3 (OP2, SRL, Sub, And, Nor, SLT);
  or or_4 (OP3, SRA, Add, And, SLT);
endmodule

module IC2 (
  input  op0,
  input  op1,
  input  op2,
  input  op3,
  input  op4,
  input  op5,
  output xori,
  output sltiu,
  output sh,
  output bgtz
);

  wire not_1_out, not_2_out, not_3_out, not_4_out, not_5_out, not_6_out, not_7_out, not_8_out, not_9_out,
       not_10_out, not_11_out, not_12_out;

  not not_1 (not_1_out, op0);
  not not_2 (not_2_out, op1);
  not not_3 (not_3_out, op5);
  not not_4 (not_4_out, op0);
  not not_5 (not_5_out, op1);
  not not_6 (not_6_out, op3);
  not not_7 (not_7_out, op1);
  not not_8 (not_8_out, op3);
  not not_9 (not_9_out, op4);
  not not_10 (not_10_out, op0);
  not not_11 (not_11_out, op1);
  not not_12 (not_12_out, op2);
  and and_1 (xori, not_1_out, not_2_out, op2, op3, op4, not_3_out);
  and and_2 (sltiu, not_4_out, not_5_out, op2, not_6_out, op4, op5);
  and and_3 (sh, op0, not_7_out, op2, not_8_out, not_9_out, op5);
  and and_4 (bgtz, not_10_out, not_11_out, not_12_out, op3, op4, op5);
endmodule

module IC3 (
  input  op0,
  input  op1,
  input  op2,
  input  op3,
  input  op4,
  input  op5,
  input  funct0,
  input  funct1,
  input  funct2,
  input  funct3,
  input  funct4,
  input  funct5,
  output MFC0,
  output ERET
);

  wire not_1_out, not_2_out, not_3_out, not_4_out, not_5_out, not_6_out, not_7_out, not_8_out, not_9_out,
       not_10_out, not_11_out, not_12_out, not_13_out, not_14_out, not_15_out, not_16_out, not_17_out;

  not not_1 (not_1_out, op0);
  not not_2 (not_2_out, op2);
  not not_3 (not_3_out, op3);
  not not_4 (not_4_out, op4);
  not not_5 (not_5_out, op5);
  not not_6 (not_6_out, funct0);
  not not_7 (not_7_out, funct1);
  not not_8 (not_8_out, funct2);
  not not_9 (not_9_out, op0);
  not not_10 (not_10_out, op2);
  not not_11 (not_11_out, op3);
  not not_12 (not_12_out, op4);
  not not_13 (not_13_out, op5);
  not not_14 (not_14_out, funct0);
  not not_15 (not_15_out, funct3);
  not not_16 (not_16_out, funct4);
  not not_17 (not_17_out, funct5);
  and and_1 (MFC0, not_1_out, op1, not_2_out, not_3_out, not_4_out, not_5_out, not_6_out, not_7_out, not_8_out);
  and and_2 (ERET, not_9_out, op1, not_10_out, not_11_out, not_12_out, not_13_out, not_14_out, funct1, funct2, not_15_out, not_16_out, not_17_out);
endmodule

module IR (
  input  [2:0] oldIR,
  input  [1:0] in_2,
  input  [1:0] INT_SRC,
  output [2:0] out_4
);

  wire [1:0] priority_encoder_1_out;
  wire [2:0] and_1_out, demultiplexer_1_out1, demultiplexer_2_out1, not_1_out, or_1_out;

  Demultiplexer #(.select(2), .enable("false")) demultiplexer_1 (
    .out1(demultiplexer_1_out1[0]), .out2(demultiplexer_1_out1[1]), .out3(demultiplexer_1_out1[2]),
    .in(1'b1), .sel(INT_SRC));  // open: out0
  Demultiplexer #(.select(2), .enable("false")) demultiplexer_2 (
    .out1(demultiplexer_2_out1[0]), .out2(demultiplexer_2_out1[1]), .out3(demultiplexer_2_out1[2]),
    .in(1'b1), .sel(priority_encoder_1_out));  // open: out0
  Priority_Encoder #(.select(2)) priority_encoder_1 (
    .in1(oldIR[0]), .in2(oldIR[1]), .in3(oldIR[2]), .out(priority_encoder_1_out));  // open: in0, gs, en_out, en_in
  assign or_1_out = oldIR | demultiplexer_1_out1;  // OR_Gate or_1, 3 bits wide
  assign not_1_out = ~demultiplexer_2_out1;  // NOT_Gate not_1, 3 bits wide
  assign and_1_out = not_1_out & oldIR;  // AND_Gate and_1, 3 bits wide
  Multiplexer #(.select(2), .width(3), .enable("false")) multiplexer_1 (
    .in0(oldIR), .in1(or_1_out), .in2(and_1_out), .in3(oldIR), .out(out_4), .sel(in_2));
endmodule
