// Logisim project Cpu-Interrupt.circ as structural Verilog: 4 circuits, main circuit main
module main (
);

  wire AluSrc, and_1_out, and_2_out, Branch, Clear1, Clear2, Clear3, clk, Equal, Extype, Finish, Greater0,
       Halt, IE, INT1, INT2, INT3, INT_SIG, Jal, JmpReg, Jump, MemRead, MemToReg, MemWrite,
       multiplexer_2_out, not_1_out, not_2_out, not_3_out, not_4_out, PCtoReg, R1Src, RegDst, RegWrite,
       SelectBase, Shift, SysCall, UpdateINT, WAIT1, WAIT2, WAIT3;
  wire [1:0] INT_SRC, IR_now, register_2_q;
  wire [2:0] INM, IR_next;
  wire [3:0] AluControl;
  wire [4:0] counter_1_q, Decoder_rd, Decoder_rs, Decoder_rt, Decoder_shamt, multiplexer_4_out,
       multiplexer_5_out, multiplexer_6_out, subtractor_1_out;
  wire [5:0] Decoder_funct, Decoder_op;
  wire [15:0] Decoder_immi, main_2_reg2_2, main_2_reg2_2_2;
  wire [25:0] Decoder_immj;
  wire [31:0] adder_1_out, adder_2_out, bit_extender_2_out, bit_extender_3_out, counter_2_q, display,
       main_2_out_13, main_2_out_14, multiplexer_1_out, multiplexer_3_out, multiplexer_7_out,
       multiplexer_8_out, multiplexer_9_out, multiplexer_10_out, multiplexer_11_out, multiplexer_12_out,
       multiplexer_14_out, multiplexer_15_out, PC_Next, PC_q, PC_Store, ram_2_data, Reg, register_1_q,
       rom_1_data, Sh, shifter_1_out;
  wire [31:1] alu_1_result;

  Button _1 (.out(INT1));
  Button _2 (.out(INT2));
  Button _3 (.out(INT3));
  Clock #(.highDuration(2), .lowDuration(2)) clock_1 (.out(clk));
  not not_1 (not_1_out, and_1_out);
  and and_1 (and_1_out, Halt, SysCall);
  or or_1 (UpdateINT, Finish, multiplexer_2_out);
  Hex_Digit_Display hex_digit_display_1 (.value(display[31:28]));  // open: dp
  Hex_Digit_Display hex_digit_display_2 (.value(display[27:24]));  // open: dp
  LED led_1 (.in(WAIT1));
  LED led_2 (.in(WAIT2));
  LED led_3 (.in(WAIT3));
  Register #(.width(32), .trigger("falling")) PC (
    .D(multiplexer_1_out), .en(not_1_out), .Q(PC_q), .clk(clk));  // open: clr
  Multiplexer #(.width(32), .enable("false")) multiplexer_1 (
    .in0(multiplexer_3_out), .in1(PC_Store), .out(multiplexer_1_out), .sel(Finish));
  // Probe on IR_next
  Counter #(.width(5), .max('h1f)) counter_1 (
    .load(Finish), .D(subtractor_1_out), .count(multiplexer_2_out), .Q(counter_1_q), .clk(UpdateINT));  // open: carry, clr
  Hex_Digit_Display hex_digit_display_3 (.value(display[19:16]));  // open: dp
  Hex_Digit_Display hex_digit_display_4 (.value(display[23:20]));  // open: dp
  Counter #(.width(32), .max('hffffffff)) counter_2 (
    .count(not_1_out), .Q(counter_2_q), .clk(clk));  // open: load, D, carry, clr
  // Probe on counter_2_q
  // Probe on {INM[2], IR_now}
  Register #(.width(3), .trigger("falling")) IR (.D(IR_next), .Q({INM[2], IR_now}), .clk(UpdateINT));  // open: en, clr
  Hex_Digit_Display hex_digit_display_5 (.value(display[11:8]));  // open: dp
  Hex_Digit_Display hex_digit_display_6 (.value(display[15:12]));  // open: dp
  // Probe on INT_SIG
  // Probe on INT_SRC
  ROM #(.addrWidth(10), .dataWidth(32)) rom_1 (.addr(PC_q[11:2]), .data(rom_1_data), .sel(not_1_out));
  Adder #(.width(32)) adder_1 (.a(32'h4), .b(PC_q), .out(adder_1_out));  // open: cin, cout
  Subtractor #(.width(5)) subtractor_1 (.a(counter_1_q), .b(5'b00001), .out(subtractor_1_out));  // open: bin, bout
  Multiplexer #(.select(2), .enable("false")) multiplexer_2 (
    .in0(1'b0), .in1(1'b1), .in2(1'b1), .in3(1'b1), .out(multiplexer_2_out), .sel(INT_SRC));
  Hex_Digit_Display hex_digit_display_7 (.value(display[7:4]));  // open: dp
  Hex_Digit_Display hex_digit_display_8 (.value(display[3:0]));  // open: dp
  Register #(.width(32)) register_1 (.D(rom_1_data), .Q(register_1_q), .clk(clk));  // open: en, clr
  Multiplexer #(.select(2), .width(32), .enable("false")) multiplexer_3 (
    .in0(PC_Next), .in1(32'hb0), .in2(32'h158), .in3(32'h200), .out(multiplexer_3_out), .sel(INT_SRC));
  RAM #(.addrWidth(5), .dataWidth(32), .bus("separate")) ram_1 (
    .addr(counter_1_q), .din(PC_Next), .data(PC_Store), .str(multiplexer_2_out), .clk(multiplexer_2_out),
    .ld(1'b1), .clr(1'b0));  // open: sel
  Decoder Decoder (
    .in_1(register_1_q), .OP(Decoder_op), .Rs(Decoder_rs), .Rt(Decoder_rt), .Rd(Decoder_rd),
    .Shamt(Decoder_shamt), .funct(Decoder_funct), .IMMI(Decoder_immi), .IMMJ(Decoder_immj));
  assign Sh = {{27{Decoder_shamt[4]}}, Decoder_shamt};  // Bit_Extender bit_extender_1
  assign bit_extender_2_out = {{16{Decoder_immi[15]}}, Decoder_immi};  // Bit_Extender bit_extender_2
  assign bit_extender_3_out = {{16{1'b0}}, Decoder_immi};  // Bit_Extender bit_extender_3
  Register #(.width(2)) register_2 (.D(INT_SRC), .Q(register_2_q), .clk(clk));  // open: en, clr
  or or_2 (INM[0], IR_now[0], IR_now[1], INM[2]);
  or or_3 (INM[1], IR_now[1], INM[2]);
  // Probe on Decoder_rt
  Multiplexer #(.width(5), .enable("false")) multiplexer_4 (
    .in0(Decoder_rs), .in1(Decoder_rt), .out(multiplexer_4_out), .sel(R1Src));
  Multiplexer #(.width(5), .enable("false")) multiplexer_5 (
    .in0(Decoder_rt), .in1(Decoder_rd), .out(multiplexer_5_out), .sel(RegDst));
  Multiplexer #(.width(5), .enable("false")) multiplexer_6 (
    .in0(multiplexer_5_out), .in1({5{1'b1}}), .out(multiplexer_6_out), .sel(Jal));
  // Probe on multiplexer_6_out
  Multiplexer #(.width(32)) multiplexer_7 (
    .in0(bit_extender_2_out), .in1(bit_extender_3_out), .out(multiplexer_7_out), .sel(Extype));  // open: en
  Multiplexer #(.width(32), .enable("false")) multiplexer_8 (
    .in0(multiplexer_15_out), .in1(adder_1_out), .out(multiplexer_8_out), .sel(PCtoReg));
  // Probe on INM
  Multiplexer #(.width(32)) multiplexer_9 (
    .in0({adder_1_out[31:28], Decoder_immj, 2'b00}), .in1(Reg), .out(multiplexer_9_out), .sel(JmpReg));  // open: en
  Control_main main_1 (
    .op(Decoder_op), .funct(Decoder_funct), .in_6(Equal), .AluControl(AluControl), .Extype(Extype),
    .RegDst(RegDst), .AluShift(Shift), .R1Src(R1Src), .RegWrite(RegWrite), .PCToReg(PCtoReg), .W31(Jal),
    .Jump(Jump), .AluSrc(AluSrc), .Branch(Branch), .MemWrite(MemWrite), .MemRead(MemRead), .SysCall(SysCall),
    .MemToReg(MemToReg), .JmpReg(JmpReg), .Greater0(Greater0), .SelectBase(SelectBase), .IE(IE),
    .INT_SRC(register_2_q), .Clear({Clear3, Clear2, Clear1}), .Finish(Finish), .oldIR({INM[2], IR_now}),
    .newIR(IR_next));
  Regfile_main main_2 (
    .Reg1_num(multiplexer_4_out), .Reg2(Decoder_rt), .Write_Reg_num(multiplexer_6_out),
    .Din(multiplexer_8_out), .Write_Enable(RegWrite), .Clock(not_2_out), .Reg1(Reg),
    .Reg2_2({main_2_reg2_2_2, main_2_reg2_2}), .out_13(main_2_out_13), .out_14(main_2_out_14));  // open: s0_Value, s1_Value, s2_Value, ra_Value
  not not_2 (not_2_out, clk);
  Multiplexer #(.width(32)) multiplexer_10 (
    .in0({main_2_reg2_2_2, main_2_reg2_2}), .in1(multiplexer_7_out), .out(multiplexer_10_out), .sel(AluSrc));  // open: en
  Shifter #(.width(32)) shifter_1 (.in(multiplexer_7_out), .\dist (5'b00010), .out(shifter_1_out));
  interrupt interrupt_1 (
    .clk(clk), .int1(INT1), .out_12(WAIT1), .int2(INT2), .out_13(WAIT2), .int3(INT3), .out_14(WAIT3),
    .IE(IE), .out_15(INT_SRC), .out_16(INT_SIG), .in_5(Clear3), .in_6(Clear2), .in_7(Clear1), .INM1(INM[2]),
    .INM2(INM[1]), .INM3(INM[0]));
  Multiplexer #(.width(32)) multiplexer_11 (
    .in0(multiplexer_10_out), .in1(Sh), .out(multiplexer_11_out), .sel(Shift));  // open: en
  Adder #(.width(32)) adder_2 (.a(shifter_1_out), .b(adder_1_out), .out(adder_2_out));  // open: cin, cout
  // Probe on Reg
  Multiplexer #(.width(32)) multiplexer_12 (
    .in0(adder_1_out), .in1(adder_2_out), .out(multiplexer_12_out), .sel(Branch));  // open: en
  ALU alu_1 (
    .AluOP(AluControl), .X(Reg), .Equal(Equal), .Result({alu_1_result, Greater0}), .Y(multiplexer_11_out));  // open: Signed_Overflow_350b0444, Result_2_406f29fe, UnSigned_Overflow_28bd2ab2
  Multiplexer #(.width(32)) multiplexer_13 (
    .in0(multiplexer_12_out), .in1(multiplexer_9_out), .out(PC_Next), .sel(Jump));  // open: en
  Comparator #(.width(32)) comparator_1 (.a(32'ha), .b(main_2_out_13), .eq(Halt));  // open: gt, lt
  Multiplexer #(.width(32), .enable("false")) multiplexer_14 (
    .in0({main_2_reg2_2_2, main_2_reg2_2}), .in1({{16{1'b0}}, main_2_reg2_2}), .out(multiplexer_14_out),
    .sel(SelectBase));
  not not_3 (not_3_out, Halt);
  Register #(.width(32)) register_3 (.D(main_2_out_14), .en(and_2_out), .Q(display), .clk(clk));  // open: clr
  and and_2 (and_2_out, not_3_out, SysCall);
  RAM #(.addrWidth(10), .dataWidth(32), .bus("separate")) ram_2 (
    .addr(alu_1_result[11:2]), .din(multiplexer_14_out), .data(ram_2_data), .str(MemWrite), .sel(1'b1),
    .clk(not_4_out), .ld(MemRead), .clr(1'b0));
  not not_4 (not_4_out, clk);
  Multiplexer #(.width(32)) multiplexer_15 (
    .in0({alu_1_result, Greater0}), .in1(ram_2_data), .out(multiplexer_15_out), .sel(MemToReg));  // open: en
  Hex_Digit_Display hex_digit_display_9 (.value(display[31:28]));  // open: dp
  Hex_Digit_Display hex_digit_display_10 (.value(display[27:24]));  // open: dp
  Hex_Digit_Display hex_digit_display_11 (.value(display[19:16]));  // open: dp
  Hex_Digit_Display hex_digit_display_12 (.value(display[23:20]));  // open: dp
  Hex_Digit_Display hex_digit_display_13 (.value(display[15:12]));  // open: dp
  Hex_Digit_Display hex_digit_display_14 (.value(display[11:8]));  // open: dp
  Hex_Digit_Display hex_digit_display_15 (.value(display[7:4]));  // open: dp
  Hex_Digit_Display hex_digit_display_16 (.value(display[3:0]));  // open: dp
  // also tied to VCC on the sheet: IE

  // Other names for the same wires on the sheet: IR_now[2] = INM[2]; per = clk

  // Notes on the sheet:
  //   contents of rom_1 (hex, n*v repeats v):
  //   241d0064 20100001 109fc0 139fc3 8021 2012000c 24160003 26100001 3210000f 20080008 20090001 139900
  //   2709825 132020 20020022 c 1094022 1500fff9 22100001 2018000f 2188024 108700 20080008 20090001 139902
  //   2709825 132021 20020022 c 1094022 1500fff9 108702 2c9b022 12c00001 8000c07 4020 1084027 84400
  //   3508ffff 82021 20020022 c 2002000a c 40119000 27bdfffc afb00000 27bdfffc afb30000 27bdfffc afb40000
  //   27bdfffc afb50000 27bdfffc afb60000 27bdfffc afa40000 27bdfffc afa20000 20160001 20140006 20150001
  //   168020 108100 2149825 132020 20020022 c 1600fffa 295a022 1680fff7 8fa20000 27bd0004 8fa40000
  //   27bd0004 8fb60000 27bd0004 8fb50000 27bd0004 8fb40000 27bd0004 8fb30000 27bd0004 8fb00000 27bd0004
  //   42000018 40119000 27bdfffc afb00000 27bdfffc afb30000 27bdfffc afb40000 27bdfffc afb50000 27bdfffc
  //   afb60000 27bdfffc afa40000 27bdfffc afa20000 20160002 20140006 20150001 168020 108100 2149825 132020
  //   20020022 c 1600fffa 295a022 1680fff7 8fa20000 27bd0004 8fa40000 27bd0004 8fb60000 27bd0004 8fb50000
  //   27bd0004 8fb40000 27bd0004 8fb30000 27bd0004 8fb00000 27bd0004 42000018 40119000 27bdfffc afb00000
  //   27bdfffc afb30000 27bdfffc afb40000 27bdfffc afb50000 27bdfffc afb60000 27bdfffc afa40000 27bdfffc
  //   afa20000 20160003 20140006 20150001 168020 108100 2149825 132020 20020022 c 1600fffa 295a022
  //   1680fff7 8fa20000 27bd0004 8fa40000 27bd0004 8fb60000 27bd0004 8fb50000 27bd0004 8fb40000 27bd0004
  //   8fb30000 27bd0004 8fb00000 27bd0004 42000018
endmodule

module Decoder (
  input  [31:0] in_1,
  output [5:0] OP,
  output [4:0] Rs,
  output [4:0] Rt,
  output [4:0] Rd,
  output [4:0] Shamt,
  output [5:0] funct,
  output [15:0] IMMI,
  output [25:0] IMMJ
);


  assign funct = in_1[5:0];
  assign IMMI = in_1[15:0];
  assign IMMJ = in_1[25:0];
  assign OP = in_1[31:26];
  assign Rd = in_1[15:11];
  assign Rs = in_1[25:21];
  assign Rt = in_1[20:16];
  assign Shamt = in_1[10:6];
endmodule

module interrupt (
  input  clk,
  input  int1,
  input  int2,
  input  int3,
  input  in_5,
  input  in_6,
  input  in_7,
  input  IE,
  input  INM3,
  input  INM2,
  input  INM1,
  output out_12,
  output out_13,
  output out_14,
  output [1:0] out_15,
  output out_16
);

  wire and_1_out, and_2_out, and_3_out, \int_signal_1_中断屏蔽位 , \int_signal_2_中断屏蔽位 , \int_signal_3_中断屏蔽位 ,
       not_1_out, not_2_out, not_3_out, priority_encoder_1_gs;

  not not_1 (not_1_out, INM3);
  not not_2 (not_2_out, INM2);
  not not_3 (not_3_out, INM1);
  int_signal int_signal_1 (.\时钟 (clk), .\中断按钮 (int1), .\等待指示灯 (out_12), .\中断屏蔽位 (\int_signal_1_中断屏蔽位 ), .in_3(in_7));
  int_signal int_signal_2 (.\时钟 (clk), .\中断按钮 (int2), .\等待指示灯 (out_13), .\中断屏蔽位 (\int_signal_2_中断屏蔽位 ), .in_3(in_6));
  int_signal int_signal_3 (.\时钟 (clk), .\中断按钮 (int3), .\等待指示灯 (out_14), .\中断屏蔽位 (\int_signal_3_中断屏蔽位 ), .in_3(in_5));
  and and_1 (and_1_out, \int_signal_1_中断屏蔽位 , not_1_out);
  and and_2 (and_2_out, \int_signal_2_中断屏蔽位 , not_2_out);
  and and_3 (and_3_out, \int_signal_3_中断屏蔽位 , not_3_out);
  Priority_Encoder #(.select(2), .disabled(0)) priority_encoder_1 (
    .in0(1'b1), .in1(and_1_out), .in2(and_2_out), .in3(and_3_out), .out(out_15), .gs(priority_encoder_1_gs));  // open: en_out, en_in
  and and_4 (out_16, priority_encoder_1_gs, IE);
endmodule

module int_signal (
  input  \时钟 ,
  input  \中断按钮 ,
  input  in_3,
  output \中断屏蔽位 ,
  output \等待指示灯 
);

  wire and_1_out, d_ff_1_q, not_1_out, or_2_out;

  D_Flip_Flop #(.trigger("high")) d_ff_1 (
    .clk(\中断按钮 ), .D(1'b1), .Q(d_ff_1_q), .reset(\中断屏蔽位 ));  // open: Qn, preset, en
  or or_1 (\等待指示灯 , \中断屏蔽位 , d_ff_1_q);
  or or_2 (or_2_out, d_ff_1_q, \中断屏蔽位 );
  and and_1 (and_1_out, or_2_out, not_1_out);
  not not_1 (not_1_out, in_3);
  D_Flip_Flop #(.trigger("high")) d_ff_2 (.clk(\时钟 ), .D(and_1_out), .Q(\中断屏蔽位 ));  // open: Qn, preset, en, reset
endmodule
