// Logisim project Cpu.circ as structural Verilog: 12 circuits, main circuit main
module main (
);

  wire AluSrc, and_1_out, and_3_out, and_4_out, Branch, Branch2, Bubble, Bubble_f, Bubble_j, Clear1, Clear2,
       Clear3, clk, Equal, Equal3, Equal4, Extype, Finish, Greater0, Greater03, Greater04, Halt, Halt3,
       Halt4, IE, INT1, INT2, INT3, INT_SIG, Jal, JmpReg, Jump, Jump2, LoadUse, MemRead, MemRead2, MemRead3,
       MemToReg, MemToReg2, MemToReg3, MemToReg4, MemWrite, MemWrite2, MemWrite3, multiplexer_4_out,
       NewBranch, NewHalt, not_2_out, not_3_out, not_4_out, or_2_out, or_5_out, or_6_out, or_7_out, PCtoReg,
       PCtoReg2, PCtoReg3, PCtoReg4, R1Src, RegDst, register_1_q, register_2_q, RegWrite, RegWrite2,
       RegWrite3, RegWrite4, SelectBase, SelectBase2, Shift, SysCall, SysCall2, SysCall3, SysCall4,
       UpdateINT, WAIT1, WAIT2, WAIT3;
  wire [1:0] Bypass1, Bypass2, Bypass3, Bypass4, Bypass12, Bypass22, id_ex_1_out_51, id_ex_1_out_53, INT_SRC,
       IR_now, register_3_q;
  wire [2:0] INM, IR_next;
  wire [3:0] AluControl, AluControl2;
  wire [4:0] counter_2_q, Decoder_rd, Decoder_rs, Decoder_shamt, multiplexer_7_out, R1, R2, RW_2, RW_3, RW_4,
       RW_num, subtractor_1_out;
  wire [5:0] Decoder_funct, Decoder_op;
  wire [15:0] Decoder_immi;
  wire [25:0] Decoder_immj;
  wire [31:0] adder_1_out, adder_2_out, adder_3_out, bit_extender_2_out, bit_extender_3_out, counter_1_q,
       counter_3_q, counter_4_q, display, ex_mem_1_out_25, ex_mem_1_out_26, id_ex_1_out_39, id_ex_1_out_40,
       id_ex_1_out_41, id_ex_1_out_42, id_ex_1_out_43, id_ex_1_out_44, id_ex_1_out_45, id_ex_1_out_46,
       if_id_1_out_9, IR1, IR2, IR3, IR4, main_2_out_13, main_2_out_14, main_2_reg2_2, MEM_NM, MEM_NM_,
       multiplexer_1_out, multiplexer_2_out, multiplexer_3_out, multiplexer_5_out, multiplexer_9_out,
       multiplexer_10_out, multiplexer_11_out, multiplexer_12_out, multiplexer_13_out, multiplexer_14_out,
       multiplexer_15_out, multiplexer_16_out, multiplexer_17_out, multiplexer_19_out, multiplexer_20_out,
       multiplexer_21_out, PC0, PC1, PC2, PC3, PC4, PC_Next, PC_Store, Reg, rom_1_data, Sh, shifter_1_out,
       WB_Data, WB_Data_, WB_NM;

  Button _1 (.out(INT1));
  Button _2 (.out(INT2));
  Button _3 (.out(INT3));
  Clock #(.highDuration(2), .lowDuration(2)) clock_1 (.out(clk));
  not not_1 (NewHalt, and_1_out);
  and and_1 (and_1_out, register_1_q, register_2_q);
  Register #(.width(1)) register_1 (.D(Halt4), .en(NewHalt), .Q(register_1_q), .clk(clk));  // open: clr
  Register #(.width(1)) register_2 (.D(SysCall4), .en(NewHalt), .Q(register_2_q), .clk(clk));  // open: clr
  or or_1 (UpdateINT, Finish, multiplexer_4_out);
  Hex_Digit_Display hex_digit_display_1 (.value(display[31:28]));  // open: dp
  LED led_1 (.in(WAIT1));
  LED led_2 (.in(WAIT2));
  LED led_3 (.in(WAIT3));
  Register #(.width(32), .trigger("falling")) PC (
    .D(multiplexer_1_out), .en(NewHalt), .Q(PC0), .clk(clk));  // open: clr
  Hex_Digit_Display hex_digit_display_2 (.value(display[23:20]));  // open: dp
  Hex_Digit_Display hex_digit_display_3 (.value(display[27:24]));  // open: dp
  // Probe on INT_SIG
  // Probe on INT_SRC
  Counter #(.width(32), .max('hffffffff)) counter_1 (
    .count(NewHalt), .Q(counter_1_q), .clk(clk));  // open: load, D, carry, clr
  // Probe on counter_1_q
  // Probe on multiplexer_1_out
  Multiplexer #(.width(32), .enable("false")) multiplexer_1 (
    .in0(multiplexer_2_out), .in1(PC0), .out(multiplexer_1_out), .sel(Bubble));
  Multiplexer #(.width(32), .enable("false")) multiplexer_2 (
    .in0(adder_1_out), .in1(multiplexer_3_out), .out(multiplexer_2_out), .sel(or_2_out));
  or or_2 (or_2_out, NewBranch, Jump2);
  // Probe on IR_next
  Register #(.width(3), .trigger("falling")) IR (.D(IR_next), .Q({INM[2], IR_now}), .clk(UpdateINT));  // open: en, clr
  Counter #(.width(5), .max('h1f)) counter_2 (
    .load(Finish), .D(subtractor_1_out), .count(multiplexer_4_out), .Q(counter_2_q), .clk(UpdateINT));  // open: carry, clr
  Hex_Digit_Display hex_digit_display_4 (.value(display[15:12]));  // open: dp
  Hex_Digit_Display hex_digit_display_5 (.value(display[19:16]));  // open: dp
  Multiplexer #(.width(32), .enable("false")) multiplexer_3 (
    .in0(multiplexer_5_out), .in1(PC_Store), .out(multiplexer_3_out), .sel(Finish));
  // Probe on {INM[2], IR_now}
  Subtractor #(.width(5)) subtractor_1 (.a(counter_2_q), .b(5'b00001), .out(subtractor_1_out));  // open: bin, bout
  Multiplexer #(.select(2), .enable("false")) multiplexer_4 (
    .in0(1'b0), .in1(1'b1), .in2(1'b1), .in3(1'b1), .out(multiplexer_4_out), .sel(INT_SRC));
  Hex_Digit_Display hex_digit_display_6 (.value(display[7:4]));  // open: dp
  Hex_Digit_Display hex_digit_display_7 (.value(display[11:8]));  // open: dp
  IF_ID if_id_1 (
    .in_1(clk), .in_2(PC0), .in_3(rom_1_data), .in_4(adder_1_out), .out_7(PC1), .out_8(IR1),
    .out_9(if_id_1_out_9), .in_6(NewHalt), .Bubble(Bubble_j));
  ROM #(.addrWidth(10), .dataWidth(32)) rom_1 (.addr(PC0[11:2]), .data(rom_1_data), .sel(NewHalt));
  Adder #(.width(32)) adder_1 (.a(32'h4), .b(PC0), .out(adder_1_out));  // open: cin, cout
  RAM #(.addrWidth(5), .dataWidth(32), .bus("separate")) ram_1 (
    .addr(counter_2_q), .din(PC_Next), .data(PC_Store), .str(multiplexer_4_out), .clk(multiplexer_4_out),
    .ld(1'b1), .clr(1'b0));  // open: sel
  Hex_Digit_Display hex_digit_display_8 (.value(display[3:0]));  // open: dp
  Decoder Decoder (
    .in_1(IR1), .OP(Decoder_op), .Rs(Decoder_rs), .Rt(R2), .Rd(Decoder_rd), .Shamt(Decoder_shamt),
    .funct(Decoder_funct), .IMMI(Decoder_immi), .IMMJ(Decoder_immj));
  // Probe on if_id_1_out_9
  Multiplexer #(.select(2), .width(32), .enable("false")) multiplexer_5 (
    .in0(PC_Next), .in1(32'hb0), .in2(32'h158), .in3(32'h200), .out(multiplexer_5_out), .sel(INT_SRC));
  Register #(.width(2)) register_3 (.D(INT_SRC), .Q(register_3_q), .clk(clk));  // open: en, clr
  assign Sh = {{27{Decoder_shamt[4]}}, Decoder_shamt};  // Bit_Extender bit_extender_1
  assign bit_extender_2_out = {{16{Decoder_immi[15]}}, Decoder_immi};  // Bit_Extender bit_extender_2
  assign bit_extender_3_out = {{16{1'b0}}, Decoder_immi};  // Bit_Extender bit_extender_3
  or or_3 (INM[0], IR_now[0], IR_now[1], INM[2]);
  or or_4 (INM[1], IR_now[1], INM[2]);
  Multiplexer #(.width(5), .enable("false")) multiplexer_6 (.in0(Decoder_rs), .in1(R2), .out(R1), .sel(R1Src));
  Multiplexer #(.width(5), .enable("false")) multiplexer_7 (
    .in0(R2), .in1(Decoder_rd), .out(multiplexer_7_out), .sel(RegDst));
  Multiplexer #(.width(5), .enable("false")) multiplexer_8 (
    .in0(multiplexer_7_out), .in1({5{1'b1}}), .out(RW_num), .sel(Jal));
  // Probe on INM
  interrupt interrupt_1 (
    .clk(clk), .int1(INT1), .out_12(WAIT1), .int2(INT2), .out_13(WAIT2), .int3(INT3), .out_14(WAIT3),
    .IE(IE), .out_15(INT_SRC), .out_16(INT_SIG), .in_5(Clear3), .in_6(Clear2), .in_7(Clear1), .INM1(INM[2]),
    .INM2(INM[1]), .INM3(INM[0]));
  // Probe on RW_4
  Multiplexer #(.width(32), .enable("false")) multiplexer_9 (
    .in0(bit_extender_2_out), .in1(bit_extender_3_out), .out(multiplexer_9_out), .sel(Extype));
  Adder #(.width(32)) adder_2 (.a(32'h4), .b(PC4), .out(adder_2_out));  // open: cin, cout
  Control_main main_1 (
    .op(Decoder_op), .funct(Decoder_funct), .in_6(Equal4), .AluControl(AluControl), .Extype(Extype),
    .RegDst(RegDst), .AluShift(Shift), .R1Src(R1Src), .RegWrite(RegWrite), .PCToReg(PCtoReg), .W31(Jal),
    .Jump(Jump), .AluSrc(AluSrc), .Branch(Branch), .MemWrite(MemWrite), .MemRead(MemRead), .SysCall(SysCall),
    .MemToReg(MemToReg), .JmpReg(JmpReg), .Greater0(Greater04), .SelectBase(SelectBase), .IE(IE),
    .INT_SRC(register_3_q), .Clear({Clear3, Clear2, Clear1}), .Finish(Finish), .oldIR({INM[2], IR_now}),
    .newIR(IR_next));
  Regfile_main main_2 (
    .Reg1_num(R1), .Reg2(R2), .Write_Reg_num(RW_4), .Din(multiplexer_10_out), .Write_Enable(RegWrite4),
    .Clock(not_2_out), .Reg1(Reg), .Reg2_2(main_2_reg2_2), .out_13(main_2_out_13), .out_14(main_2_out_14));  // open: s0_Value, s1_Value, s2_Value, ra_Value
  Multiplexer #(.width(32), .enable("false")) multiplexer_10 (
    .in0(multiplexer_21_out), .in1(adder_2_out), .out(multiplexer_10_out), .sel(PCtoReg4));
  not not_2 (not_2_out, clk);
  or or_5 (or_5_out, ~RegDst, R1Src);  // OR_Gate
  // Probe on Bypass1
  // Probe on IR1
  Multiplexer #(.select(2), .width(32), .enable("false")) multiplexer_11 (
    .in0(main_2_reg2_2), .in1(MEM_NM_), .in2(MEM_NM), .in3(WB_Data_), .out(multiplexer_11_out), .sel(Bypass2));
  Multiplexer #(.width(32), .enable("false")) multiplexer_12 (
    .in0({if_id_1_out_9[31:28], Decoder_immj, 2'b00}), .in1(Reg), .out(multiplexer_12_out), .sel(JmpReg));
  redirect redirect_1 (
    .in_1(R1), .in_2(R2), .in_3(IR1), .in_4(RW_2), .in_5(RW_3), .in_6(NewBranch), .in_7(JmpReg), .in_8(Jump),
    .in_9(MemRead3), .out_13(Bypass1), .out_14(Bypass3), .out_15(Bypass2), .out_16(Bypass4),
    .out_17(Bubble_f), .out_19(Bubble), .out_20(LoadUse), .in_10(RegWrite2), .in_11(RegWrite3),
    .in_12(or_5_out), .out_18(Bubble_j));
  // Probe on Bypass3
  or or_6 (or_6_out, Bubble, Bubble_f);
  Multiplexer #(.width(32), .enable("false")) multiplexer_13 (
    .in0(multiplexer_11_out), .in1(multiplexer_9_out), .out(multiplexer_13_out), .sel(AluSrc));
  // Probe on Bypass2
  ID_EX id_ex_1 (
    .in_3(MemWrite), .in_4(MemRead), .in_5(SelectBase), .in_6(SysCall), .in_8(Branch), .in_9(AluControl),
    .in_10(Jump), .in_11(PC1), .in_12(IR1), .in_13(main_2_out_13), .in_14(main_2_out_14), .in_15(Reg),
    .in_16(multiplexer_14_out), .in_17(multiplexer_11_out), .in_18(multiplexer_9_out), .in_19(if_id_1_out_9),
    .in_20(multiplexer_12_out), .out_29(MemWrite2), .out_30(MemRead2), .out_31(SelectBase2),
    .out_32(SysCall2), .out_33(MemToReg2), .out_34(Branch2), .out_35(AluControl2), .out_36(Jump2),
    .out_37(PC2), .out_38(IR2), .out_39(id_ex_1_out_39), .out_40(id_ex_1_out_40), .out_41(id_ex_1_out_41),
    .out_42(id_ex_1_out_42), .out_43(id_ex_1_out_43), .out_44(id_ex_1_out_44), .out_45(id_ex_1_out_45),
    .out_46(id_ex_1_out_46), .clk(clk), .in_21(RegWrite), .out_47(RegWrite2), .in_23(RW_num), .out_49(RW_2),
    .in_26(PCtoReg), .out_52(PCtoReg2), .in_28(NewHalt), .Bubble(or_6_out), .in_7(MemToReg), .in_22(Bypass1),
    .out_48(Bypass12), .out_50(Bypass22), .out_51(id_ex_1_out_51), .out_53(id_ex_1_out_53), .in_24(Bypass2),
    .in_25(Bypass3), .in_27(Bypass4));
  Multiplexer #(.width(32), .enable("false")) multiplexer_14 (
    .in0(multiplexer_13_out), .in1(Sh), .out(multiplexer_14_out), .sel(Shift));
  // Probe on Bypass4
  Shifter #(.width(32)) shifter_1 (.in(id_ex_1_out_44), .\dist (5'b00010), .out(shifter_1_out));
  Multiplexer #(.select(2), .width(32), .enable("false")) multiplexer_15 (
    .in0(id_ex_1_out_41), .in1(MEM_NM), .in2(WB_NM), .in3(WB_Data), .out(multiplexer_15_out), .sel(Bypass12));
  Multiplexer #(.width(32), .enable("false")) multiplexer_16 (
    .in0(id_ex_1_out_43), .in1({{16{1'b0}}, id_ex_1_out_43[15:0]}), .out(multiplexer_16_out),
    .sel(SelectBase2));
  Adder #(.width(32)) adder_3 (.a(shifter_1_out), .b(id_ex_1_out_45), .out(adder_3_out));  // open: cin, cout
  and and_2 (Greater0, ~MEM_NM_[0], ~Equal);  // AND_Gate
  ALU alu_1 (
    .AluOP(AluControl2), .X(multiplexer_15_out), .Equal(Equal), .Result(MEM_NM_), .Y(id_ex_1_out_42));  // open: Signed_Overflow_350b0444, Result_2_406f29fe, UnSigned_Overflow_28bd2ab2
  // Probe on IR2
  Multiplexer #(.width(32), .enable("false")) multiplexer_17 (
    .in0(id_ex_1_out_45), .in1(adder_3_out), .out(multiplexer_17_out), .sel(NewBranch));
  Multiplexer #(.width(32), .enable("false")) multiplexer_18 (
    .in0(multiplexer_17_out), .in1(id_ex_1_out_46), .out(PC_Next), .sel(Jump2));
  Multiplexer #(.select(2), .width(32), .enable("false")) multiplexer_19 (
    .in0(id_ex_1_out_39), .in1(MEM_NM), .in2(WB_NM), .in3(WB_Data), .out(multiplexer_19_out),
    .sel(id_ex_1_out_51));
  EX_MEM ex_mem_1 (
    .in_2(Equal), .in_3(SysCall2), .in_4(Halt), .in_5(MemToReg2), .in_6(MemWrite2), .in_7(MemRead2),
    .in_8(MEM_NM_), .in_9(MEM_NM_), .in_10(multiplexer_16_out), .out_18(Equal3), .out_19(SysCall3),
    .out_20(Halt3), .out_21(MemToReg3), .out_22(MemWrite3), .out_23(MemRead3), .out_24(MEM_NM),
    .out_25(ex_mem_1_out_25), .out_26(ex_mem_1_out_26), .in_11(PC2), .out_27(PC3), .in_12(IR2), .out_28(IR3),
    .Clk(clk), .in_13(RegWrite2), .out_29(RegWrite3), .in_14(RW_2), .out_30(RW_3), .in_15(Greater0),
    .out_31(Greater03), .out_32(PCtoReg3), .in_16(PCtoReg2), .in_17(NewHalt));
  // Probe on PC_Next
  Multiplexer #(.select(2), .width(32), .enable("false")) multiplexer_20 (
    .in0(id_ex_1_out_40), .in1(MEM_NM), .in2(WB_NM), .in3(WB_Data), .out(multiplexer_20_out),
    .sel(id_ex_1_out_53));
  Register #(.width(32)) register_4 (.D(multiplexer_20_out), .en(and_4_out), .Q(display), .clk(clk));  // open: clr
  // Probe on counter_3_q
  Counter #(.width(32), .max('hffffffff)) counter_3 (
    .count(1'b1), .Q(counter_3_q), .clk(LoadUse));  // open: load, D, carry, clr
  and and_3 (and_3_out, Branch2, NewBranch);
  not not_3 (not_3_out, Halt);
  Comparator #(.width(32)) comparator_1 (.a(32'ha), .b(multiplexer_19_out), .eq(Halt));  // open: gt, lt
  // Probe on IR3
  Counter #(.width(32), .max('hffffffff)) counter_4 (
    .count(or_7_out), .Q(counter_4_q), .clk(clk));  // open: load, D, carry, clr
  or or_7 (or_7_out, and_3_out, Jump2);
  and and_4 (and_4_out, not_3_out, SysCall2);
  IR_Branch ir_branch_1 (._0(Greater0), .Equal(Equal), .IR(IR2), .Branch(NewBranch));
  Hex_Digit_Display hex_digit_display_9 (.value(display[31:28]));  // open: dp
  Hex_Digit_Display hex_digit_display_10 (.value(display[27:24]));  // open: dp
  // Probe on counter_4_q
  RAM #(.addrWidth(10), .dataWidth(32), .bus("separate")) ram_2 (
    .addr(ex_mem_1_out_25[11:2]), .din(ex_mem_1_out_26), .data(WB_Data_), .str(MemWrite3), .sel(1'b1),
    .clk(not_4_out), .ld(MemRead3), .clr(1'b0));
  not not_4 (not_4_out, clk);
  Hex_Digit_Display hex_digit_display_11 (.value(display[19:16]));  // open: dp
  Hex_Digit_Display hex_digit_display_12 (.value(display[23:20]));  // open: dp
  MEM_WB mem_wb_1 (
    .Clk(clk), .in_2(Equal3), .in_3(SysCall3), .in_4(Halt3), .in_5(MemToReg3), .in_6(MEM_NM),
    .in_7(WB_Data_), .in_8(PC3), .in_9(IR3), .in_10(RegWrite3), .in_11(RW_3), .in_12(Greater03),
    .in_13(PCtoReg3), .out_15(Equal4), .out_16(SysCall4), .out_17(Halt4), .out_18(MemToReg4), .out_19(WB_NM),
    .out_20(WB_Data), .out_21(PC4), .out_22(IR4), .out_23(RegWrite4), .out_24(RW_4), .out_25(Greater04),
    .out_26(PCtoReg4), .in_14(NewHalt));
  Hex_Digit_Display hex_digit_display_13 (.value(display[11:8]));  // open: dp
  Hex_Digit_Display hex_digit_display_14 (.value(display[15:12]));  // open: dp
  Hex_Digit_Display hex_digit_display_15 (.value(display[7:4]));  // open: dp
  Hex_Digit_Display hex_digit_display_16 (.value(display[3:0]));  // open: dp
  Multiplexer #(.width(32), .enable("false")) multiplexer_21 (
    .in0(WB_NM), .in1(WB_Data), .out(multiplexer_21_out), .sel(MemToReg4));

  // Other names for the same wires on the sheet: IR_now[2] = INM[2]; per = clk; WB_NM_[31:0] = MEM_NM

  // Notes on the sheet:
  //   contents of rom_1 (hex, n*v repeats v):
  //   20110001 8000c05 20110001 20120002 20130003 8000c09 20110001 20120002 20130003 8000c0d 20110001
  //   20120002 20130003 8000c11 20110001 20120002 20130003 c000cb8 20100001 20110001 118fc0 112020
  //   20020022 c 118882 12200001 8000c15 112020 20020022 c 20110001 118880 112020 20020022 c 12200001
  //   8000c1f 20110001 118fc0 112020 20020022 c 1188c3 112020 20020022 c 118903 112020 20020022 c 118903
  //   112020 20020022 c 118903 112020 20020022 c 118903 112020 20020022 c 118903 112020 20020022 c 118903
  //   112020 20020022 c 118903 112020 20020022 c 20100001 109fc0 139fc3 8021 2012000c 24160003 26100001
  //   3210000f 20080008 20090001 139900 2709825 132020 20020022 c 1094022 1500fff9 22100001 2018000f
  //   2188024 108700 20080008 20090001 139902 2709825 132021 20020022 c 1094022 1500fff9 108702 2c9b022
  //   12c00001 8000c50 4020 1084027 84400 3508ffff 82021 20020022 c 2010ffff 20110000 ae300000 22100001
  //   22310004 ae300000 22100001 22310004 ae300000 22100001 22310004 ae300000 22100001 22310004 ae300000
  //   22100001 22310004 ae300000 22100001 22310004 ae300000 22100001 22310004 ae300000 22100001 22310004
  //   ae300000 22100001 22310004 ae300000 22100001 22310004 ae300000 22100001 22310004 ae300000 22100001
  //   22310004 ae300000 22100001 22310004 ae300000 22100001 22310004 ae300000 22100001 22310004 ae300000
  //   22100001 22310004 22100001 8020 2011003c 8e130000 8e340000 274402a 11000002 ae330000 ae140000
  //   2231fffc 1611fff8 102020 20020022 c 22100004 2011003c 1611fff2 2002000a c 20100000 22100001 102020
  //   20020022 c 22100002 102020 20020022 c 22100003 102020 20020022 c 22100004 102020 20020022 c 22100005
  //   102020 20020022 c 22100006 102020 20020022 c 22100007 102020 20020022 c 22100008 102020 20020022
  //   20020022 c 3e00008
endmodule

module Decoder (
  input  [31:0] in_1,
  output [5:0] OP,
  output [4:0] Rs,
  output [4:0] Rt,
  output [4:0] Rd,
  output [4:0] Shamt,
  output [5:0] funct,
  output [15:0] IMMI,
  output [25:0] IMMJ
);


  assign funct = in_1[5:0];
  assign IMMI = in_1[15:0];
  assign IMMJ = in_1[25:0];
  assign OP = in_1[31:26];
  assign Rd = in_1[15:11];
  assign Rs = in_1[25:21];
  assign Rt = in_1[20:16];
  assign Shamt = in_1[10:6];
endmodule

module interrupt (
  input  clk,
  input  int1,
  input  int2,
  input  int3,
  input  in_5,
  input  in_6,
  input  in_7,
  input  IE,
  input  INM3,
  input  INM2,
  input  INM1,
  output out_12,
  output out_13,
  output out_14,
  output [1:0] out_15,
  output out_16
);

  wire and_1_out, and_2_out, and_3_out, \int_signal_1_中断屏蔽位 , \int_signal_2_中断屏蔽位 , \int_signal_3_中断屏蔽位 ,
       not_1_out, not_2_out, not_3_out, priority_encoder_1_gs;

  not not_1 (not_1_out, INM3);
  not not_2 (not_2_out, INM2);
  not not_3 (not_3_out, INM1);
  int_signal int_signal_1 (.\时钟 (clk), .\中断按钮 (int1), .\等待指示灯 (out_12), .\中断屏蔽位 (\int_signal_1_中断屏蔽位 ), .in_3(in_7));
  int_signal int_signal_2 (.\时钟 (clk), .\中断按钮 (int2), .\等待指示灯 (out_13), .\中断屏蔽位 (\int_signal_2_中断屏蔽位 ), .in_3(in_6));
  int_signal int_signal_3 (.\时钟 (clk), .\中断按钮 (int3), .\等待指示灯 (out_14), .\中断屏蔽位 (\int_signal_3_中断屏蔽位 ), .in_3(in_5));
  and and_1 (and_1_out, \int_signal_1_中断屏蔽位 , not_1_out);
  and and_2 (and_2_out, \int_signal_2_中断屏蔽位 , not_2_out);
  and and_3 (and_3_out, \int_signal_3_中断屏蔽位 , not_3_out);
  Priority_Encoder #(.select(2), .disabled(0)) priority_encoder_1 (
    .in0(1'b1), .in1(and_1_out), .in2(and_2_out), .in3(and_3_out), .out(out_15), .gs(priority_encoder_1_gs));  // open: en_out, en_in
  and and_4 (out_16, priority_encoder_1_gs, IE);
endmodule

module int_signal (
  input  \时钟 ,
  input  \中断按钮 ,
  input  in_3,
  output \中断屏蔽位 ,
  output \等待指示灯 
);

  wire and_1_out, d_ff_1_q, not_1_out, or_2_out;

  D_Flip_Flop #(.trigger("high")) d_ff_1 (
    .clk(\中断按钮 ), .D(1'b1), .Q(d_ff_1_q), .reset(\中断屏蔽位 ));  // open: Qn, preset, en
  or or_1 (\等待指示灯 , \中断屏蔽位 , d_ff_1_q);
  or or_2 (or_2_out, d_ff_1_q, \中断屏蔽位 );
  and and_1 (and_1_out, or_2_out, not_1_out);
  not not_1 (not_1_out, in_3);
  D_Flip_Flop #(.trigger("high")) d_ff_2 (.clk(\时钟 ), .D(and_1_out), .Q(\中断屏蔽位 ));  // open: Qn, preset, en, reset
endmodule

module ID_EX (
  input  Bubble,
  input  clk,
  input  in_3,
  input  in_4,
  input  in_5,
  input  in_6,
  input  in_7,
  input  in_8,
  input  [3:0] in_9,
  input  in_10,
  input  [31:0] in_11,
  input  [31:0] in_12,
  input  [31:0] in_13,
  input  [31:0] in_14,
  input  [31:0] in_15,
  input  [31:0] in_16,
  input  [31:0] in_17,
  input  [31:0] in_18,
  input  [31:0] in_19,
  input  [31:0] in_20,
  input  in_21,
  input  [1:0] in_22,
  input  [4:0] in_23,
  input  [1:0] in_24,
  input  [1:0] in_25,
  input  in_26,
  input  [1:0] in_27,
  input  in_28,
  output out_29,
  output out_30,
  output out_31,
  output out_32,
  output out_33,
  output out_34,
  output [3:0] out_35,
  output out_36,
  output [31:0] out_37,
  output [31:0] out_38,
  output [31:0] out_39,
  output [31:0] out_40,
  output [31:0] out_41,
  output [31:0] out_42,
  output [31:0] out_43,
  output [31:0] out_44,
  output [31:0] out_45,
  output [31:0] out_46,
  output out_47,
  output [1:0] out_48,
  output [4:0] out_49,
  output [1:0] out_50,
  output [1:0] out_51,
  output out_52,
  output [1:0] out_53
);

  wire multiplexer_2_out, multiplexer_3_out, multiplexer_4_out, multiplexer_6_out, multiplexer_8_out,
       multiplexer_9_out, multiplexer_10_out, multiplexer_11_out, multiplexer_12_out;
  wire [1:0] multiplexer_13_out, multiplexer_14_out, multiplexer_15_out, multiplexer_16_out;
  wire [3:0] multiplexer_5_out;
  wire [4:0] multiplexer_7_out;
  wire [31:0] multiplexer_1_out;

  Multiplexer #(.width(32), .enable("false")) multiplexer_1 (
    .in0(in_12), .in1({32{1'b0}}), .out(multiplexer_1_out), .sel(Bubble));
  Multiplexer #(.enable("false")) multiplexer_2 (.in0(in_3), .in1(1'b0), .out(multiplexer_2_out), .sel(Bubble));
  Multiplexer #(.enable("false")) multiplexer_3 (.in0(in_5), .in1(1'b0), .out(multiplexer_3_out), .sel(Bubble));
  Multiplexer #(.enable("false")) multiplexer_4 (.in0(in_7), .in1(1'b0), .out(multiplexer_4_out), .sel(Bubble));
  Multiplexer #(.width(4), .enable("false")) multiplexer_5 (
    .in0(in_9), .in1(4'b0000), .out(multiplexer_5_out), .sel(Bubble));
  Multiplexer #(.enable("false")) multiplexer_6 (.in0(in_21), .in1(1'b0), .out(multiplexer_6_out), .sel(Bubble));
  Multiplexer #(.width(5), .enable("false")) multiplexer_7 (
    .in0(in_23), .in1({5{1'b0}}), .out(multiplexer_7_out), .sel(Bubble));
  Multiplexer #(.enable("false")) multiplexer_8 (.in0(in_26), .in1(1'b0), .out(multiplexer_8_out), .sel(Bubble));
  Register #(.width(1)) MemWrite (.D(multiplexer_2_out), .en(in_28), .Q(out_29), .clk(clk));  // open: clr
  Register #(.width(1)) SelectBase (.D(multiplexer_3_out), .en(in_28), .Q(out_31), .clk(clk));  // open: clr
  Register #(.width(1)) MemtoReg (.D(multiplexer_4_out), .en(in_28), .Q(out_33), .clk(clk));  // open: clr
  Register #(.width(4)) ALUcontrol (.D(multiplexer_5_out), .en(in_28), .Q(out_35), .clk(clk));  // open: clr
  Register #(.width(32)) PC (.D(in_11), .en(in_28), .Q(out_37), .clk(clk));  // open: clr
  Register #(.width(32)) IR (.D(multiplexer_1_out), .en(in_28), .Q(out_38), .clk(clk));  // open: clr
  Register #(.width(32)) reg2 (.D(in_13), .en(in_28), .Q(out_39), .clk(clk));  // open: clr
  Register #(.width(32)) reg4 (.D(in_14), .en(in_28), .Q(out_40), .clk(clk));  // open: clr
  Register #(.width(32)) X (.D(in_15), .en(in_28), .Q(out_41), .clk(clk));  // open: clr
  Register #(.width(32)) Y (.D(in_16), .en(in_28), .Q(out_42), .clk(clk));  // open: clr
  Register #(.width(32)) RegData (.D(in_17), .en(in_28), .Q(out_43), .clk(clk));  // open: clr
  Register #(.width(32)) IMM (.D(in_18), .en(in_28), .Q(out_44), .clk(clk));  // open: clr
  Register #(.width(32)) PCnext (.D(in_19), .en(in_28), .Q(out_45), .clk(clk));  // open: clr
  Register #(.width(32)) IMMJt (.D(in_20), .en(in_28), .Q(out_46), .clk(clk));  // open: clr
  Register #(.width(1)) RegWrite (.D(multiplexer_6_out), .en(in_28), .Q(out_47), .clk(clk));  // open: clr
  Register #(.width(5)) RegDst (.D(multiplexer_7_out), .en(in_28), .Q(out_49), .clk(clk));  // open: clr
  Register #(.width(1)) PCtoReg (.D(multiplexer_8_out), .en(in_28), .Q(out_52), .clk(clk));  // open: clr
  Multiplexer #(.enable("false")) multiplexer_9 (.in0(in_4), .in1(1'b0), .out(multiplexer_9_out), .sel(Bubble));
  Multiplexer #(.enable("false")) multiplexer_10 (.in0(in_6), .in1(1'b0), .out(multiplexer_10_out), .sel(Bubble));
  Multiplexer #(.enable("false")) multiplexer_11 (.in0(in_8), .in1(1'b0), .out(multiplexer_11_out), .sel(Bubble));
  Multiplexer #(.enable("false")) multiplexer_12 (.in0(in_10), .in1(1'b0), .out(multiplexer_12_out), .sel(Bubble));
  Register #(.width(1)) MemRead (.D(multiplexer_9_out), .en(in_28), .Q(out_30), .clk(clk));  // open: clr
  Register #(.width(1)) Syscall (.D(multiplexer_10_out), .en(in_28), .Q(out_32), .clk(clk));  // open: clr
  Register #(.width(1)) Branch (.D(multiplexer_11_out), .en(in_28), .Q(out_34), .clk(clk));  // open: clr
  Register #(.width(1)) Jump (.D(multiplexer_12_out), .en(in_28), .Q(out_36), .clk(clk));  // open: clr
  Multiplexer #(.width(2), .enable("false")) multiplexer_13 (
    .in0(in_22), .in1(2'b00), .out(multiplexer_13_out), .sel(Bubble));
  Multiplexer #(.width(2), .enable("false")) multiplexer_14 (
    .in0(in_24), .in1(2'b00), .out(multiplexer_14_out), .sel(Bubble));
  Multiplexer #(.width(2), .enable("false")) multiplexer_15 (
    .in0(in_25), .in1(2'b00), .out(multiplexer_15_out), .sel(Bubble));
  Multiplexer #(.width(2), .enable("false")) multiplexer_16 (
    .in0(in_27), .in1(2'b00), .out(multiplexer_16_out), .sel(Bubble));
  Register #(.width(2)) register_1 (.D(multiplexer_13_out), .en(in_28), .Q(out_48), .clk(clk));  // open: clr
  Register #(.width(2)) register_2 (.D(multiplexer_14_out), .en(in_28), .Q(out_50), .clk(clk));  // open: clr
  Register #(.width(2)) register_3 (.D(multiplexer_15_out), .en(in_28), .Q(out_51), .clk(clk));  // open: clr
  Register #(.width(2)) register_4 (.D(multiplexer_16_out), .en(in_28), .Q(out_53), .clk(clk));  // open: clr

  // Other names for the same wires on the sheet: Halt = in_28
endmodule

module EX_MEM (
  input  Clk,
  input  in_2,
  input  in_3,
  input  in_4,
  input  in_5,
  input  in_6,
  input  in_7,
  input  [31:0] in_8,
  input  [31:0] in_9,
  input  [31:0] in_10,
  input  [31:0] in_11,
  input  [31:0] in_12,
  input  in_13,
  input  [4:0] in_14,
  input  in_15,
  input  in_16,
  input  in_17,
  output out_18,
  output out_19,
  output out_20,
  output out_21,
  output out_22,
  output out_23,
  output [31:0] out_24,
  output [31:0] out_25,
  output [31:0] out_26,
  output [31:0] out_27,
  output [31:0] out_28,
  output out_29,
  output [4:0] out_30,
  output out_31,
  output out_32
);

  Register #(.width(1)) Equal (.D(in_2), .en(in_17), .Q(out_18), .clk(Clk));  // open: clr
  Register #(.width(1)) Syscall (.D(in_3), .en(in_17), .Q(out_19), .clk(Clk));  // open: clr
  Register #(.width(1)) Halt (.D(in_4), .en(in_17), .Q(out_20), .clk(Clk));  // open: clr
  Register #(.width(1)) MemtoReg (.D(in_5), .en(in_17), .Q(out_21), .clk(Clk));  // open: clr
  Register #(.width(1)) MemWrite (.D(in_6), .en(in_17), .Q(out_22), .clk(Clk));  // open: clr
  Register #(.width(1)) MemRead (.D(in_7), .en(in_17), .Q(out_23), .clk(Clk));  // open: clr
  Register #(.width(32)) NoMem (.D(in_8), .en(in_17), .Q(out_24), .clk(Clk));  // open: clr
  Register #(.width(32)) Addr (.D(in_9), .en(in_17), .Q(out_25), .clk(Clk));  // open: clr
  Register #(.width(32)) Data (.D(in_10), .en(in_17), .Q(out_26), .clk(Clk));  // open: clr
  Register #(.width(32)) PC (.D(in_11), .en(in_17), .Q(out_27), .clk(Clk));  // open: clr
  Register #(.width(32)) IR (.D(in_12), .en(in_17), .Q(out_28), .clk(Clk));  // open: clr
  Register #(.width(1)) RegWrite (.D(in_13), .en(in_17), .Q(out_29), .clk(Clk));  // open: clr
  Register #(.width(5)) RW_num (.D(in_14), .en(in_17), .Q(out_30), .clk(Clk));  // open: clr
  Register #(.width(1)) G_0 (.D(in_15), .en(in_17), .Q(out_31), .clk(Clk));  // open: clr
  Register #(.width(1)) PCtoReg (.D(in_16), .en(in_17), .Q(out_32), .clk(Clk));  // open: clr
endmodule

module MEM_WB (
  input  Clk,
  input  in_2,
  input  in_3,
  input  in_4,
  input  in_5,
  input  [31:0] in_6,
  input  [31:0] in_7,
  input  [31:0] in_8,
  input  [31:0] in_9,
  input  in_10,
  input  [4:0] in_11,
  input  in_12,
  input  in_13,
  input  in_14,
  output out_15,
  output out_16,
  output out_17,
  output out_18,
  output [31:0] out_19,
  output [31:0] out_20,
  output [31:0] out_21,
  output [31:0] out_22,
  output out_23,
  output [4:0] out_24,
  output out_25,
  output out_26
);

  Register #(.width(1)) Equal (.D(in_2), .en(in_14), .Q(out_15), .clk(Clk));  // open: clr
  Register #(.width(1)) Syscall (.D(in_3), .en(in_14), .Q(out_16), .clk(Clk));  // open: clr
  Register #(.width(1)) Halt (.D(in_4), .en(in_14), .Q(out_17), .clk(Clk));  // open: clr
  Register #(.width(1)) MemtoReg (.D(in_5), .en(in_14), .Q(out_18), .clk(Clk));  // open: clr
  Register #(.width(32)) NoMem (.D(in_6), .en(in_14), .Q(out_19), .clk(Clk));  // open: clr
  Register #(.width(32)) Data (.D(in_7), .en(in_14), .Q(out_20), .clk(Clk));  // open: clr
  Register #(.width(32)) PC (.D(in_8), .en(in_14), .Q(out_21), .clk(Clk));  // open: clr
  Register #(.width(32)) IR (.D(in_9), .en(in_14), .Q(out_22), .clk(Clk));  // open: clr
  Register #(.width(1)) RegWrite (.D(in_10), .en(in_14), .Q(out_23), .clk(Clk));  // open: clr
  Register #(.width(5)) RW_num (.D(in_11), .en(in_14), .Q(out_24), .clk(Clk));  // open: clr
  Register #(.width(1)) _0 (.D(in_12), .en(in_14), .Q(out_25), .clk(Clk));  // open: clr
  Register #(.width(1)) PCtoReg (.D(in_13), .en(in_14), .Q(out_26), .clk(Clk));  // open: clr
endmodule

module IF_ID (
  input  in_1,
  input  [31:0] in_2,
  input  [31:0] in_3,
  input  [31:0] in_4,
  input  Bubble,
  input  in_6,
  output [31:0] out_7,
  output [31:0] out_8,
  output [31:0] out_9
);

  wire [31:0] multiplexer_1_out, multiplexer_2_out, multiplexer_3_out;

  Multiplexer #(.width(32), .enable("false")) multiplexer_1 (
    .in0(in_2), .in1({32{1'b0}}), .out(multiplexer_1_out), .sel(Bubble));
  Multiplexer #(.width(32), .enable("false")) multiplexer_2 (
    .in0(in_3), .in1({32{1'b0}}), .out(multiplexer_2_out), .sel(Bubble));
  Multiplexer #(.width(32), .enable("false")) multiplexer_3 (
    .in0(in_4), .in1({32{1'b0}}), .out(multiplexer_3_out), .sel(Bubble));
  Register #(.width(32)) PC (.D(multiplexer_1_out), .en(in_6), .Q(out_7), .clk(in_1));  // open: clr
  Register #(.width(32)) IR1 (.D(multiplexer_2_out), .en(in_6), .Q(out_8), .clk(in_1));  // open: clr
  Register #(.width(32)) PCnext1 (.D(multiplexer_3_out), .en(in_6), .Q(out_9), .clk(in_1));  // open: clr
endmodule

module IR_Branch (
  input  _0,
  input  Equal,
  input  [31:0] IR,
  output Branch
);

  wire beq, bgtz, bne, ic1_1_beq, ic1_1_bne, ic2_1_bgtz;
  wire [5:0] decoder_1_funct, decoder_1_op;

  Decoder decoder_1 (.in_1(IR), .OP(decoder_1_op), .funct(decoder_1_funct));  // open: Rs, Rt, Rd, Shamt, IMMI, IMMJ
  IC1 ic1_1 (
    .op0(decoder_1_op[5]), .op1(decoder_1_op[4]), .op2(decoder_1_op[3]), .op3(decoder_1_op[2]),
    .op4(decoder_1_op[1]), .op5(decoder_1_op[0]), .funct0(decoder_1_funct[5]), .funct1(decoder_1_funct[4]),
    .funct2(decoder_1_funct[3]), .funct3(decoder_1_funct[2]), .funct4(decoder_1_funct[1]),
    .funct5(decoder_1_funct[0]), .beq(ic1_1_beq), .bne(ic1_1_bne));  // open: nor, lw, sw, slt, slti, sltu, j, jal, jr, syscall
  IC2 ic2_1 (
    .op0(decoder_1_op[5]), .op1(decoder_1_op[4]), .op2(decoder_1_op[3]), .op3(decoder_1_op[2]),
    .op4(decoder_1_op[1]), .op5(decoder_1_op[0]), .bgtz(ic2_1_bgtz));  // open: xori, sltiu, sh
  and and_1 (beq, Equal, ic1_1_beq);
  and and_2 (bne, ic1_1_bne, ~Equal);  // AND_Gate
  and and_3 (bgtz, _0, ic2_1_bgtz);
  or or_1 (Branch, beq, bne, bgtz);
endmodule

module redirect (
  input  [4:0] in_1,
  input  [4:0] in_2,
  input  [31:0] in_3,
  input  [4:0] in_4,
  input  [4:0] in_5,
  input  in_6,
  input  in_7,
  input  in_8,
  input  in_9,
  input  in_10,
  input  in_11,
  input  in_12,
  output [1:0] out_13,
  output [1:0] out_14,
  output [1:0] out_15,
  output [1:0] out_16,
  output out_17,
  output out_18,
  output out_19,
  output out_20
);

  wire and_2_out, and_3_out, and_4_out, and_5_out, and_6_out, comparator_1_eq, comparator_2_eq,
       comparator_3_eq, comparator_4_eq, comparator_5_eq, comparator_6_eq, comparator_7_eq, comparator_8_eq,
       comparator_9_eq;
  wire [4:0] R2;

  or or_1 (out_18, in_7, in_8);
  RD1 rd1_1 (.in_1(in_1), .in_2(in_4), .in_3(in_5), .in_4(in_9), .out_7(out_13), .in_5(in_10), .in_6(in_11));
  RD1 rd1_2 (.in_1(R2), .in_2(in_4), .in_3(in_5), .in_4(in_9), .out_7(out_15), .in_5(in_10), .in_6(in_11));
  RD2 rd2_1 (
    .in_1(in_3), .in_2(in_4), .in_3(in_5), .in_4(5'b00010), .in_5(in_9), .out_8(out_14), .in_6(in_10),
    .in_7(in_11));
  RD2 rd2_2 (
    .in_1(in_3), .in_2(in_4), .in_3(in_5), .in_4(5'b00100), .in_5(in_9), .out_8(out_16), .in_6(in_10),
    .in_7(in_11));
  and and_1 (out_17, in_6, ~out_19);  // AND_Gate
  Comparator #(.width(5)) comparator_1 (.a(in_1), .b(in_2), .eq(comparator_1_eq));  // open: gt, lt
  Multiplexer #(.width(5), .enable("false")) multiplexer_1 (.in0(in_2), .in1({5{1'b0}}), .out(R2), .sel(and_2_out));
  and and_2 (and_2_out, comparator_1_eq, in_12);
  Comparator #(.width(5)) comparator_2 (.a(in_1), .b(in_4), .eq(comparator_2_eq));  // open: gt, lt
  Comparator #(.width(5)) comparator_3 (.a(in_1), .b({5{1'b0}}), .eq(comparator_3_eq));  // open: gt, lt
  Comparator #(.width(5)) comparator_4 (.a(R2), .b(in_4), .eq(comparator_4_eq));  // open: gt, lt
  Comparator #(.width(5)) comparator_5 (.a(R2), .b({5{1'b0}}), .eq(comparator_5_eq));  // open: gt, lt
  Comparator #(.width(32)) comparator_6 (.a(in_3), .b(32'hc), .eq(comparator_6_eq));  // open: gt, lt
  Comparator #(.width(5)) comparator_7 (.a(in_4), .b(5'b00010), .eq(comparator_7_eq));  // open: gt, lt
  Comparator #(.width(32)) comparator_8 (.a(in_3), .b(32'hc), .eq(comparator_8_eq));  // open: gt, lt
  Comparator #(.width(5)) comparator_9 (.a(in_4), .b(5'b00100), .eq(comparator_9_eq));  // open: gt, lt
  and and_3 (and_3_out, comparator_2_eq, ~comparator_3_eq, in_9);  // AND_Gate
  and and_4 (and_4_out, comparator_4_eq, ~comparator_5_eq, in_9);  // AND_Gate
  and and_5 (and_5_out, comparator_6_eq, comparator_7_eq, in_9);
  and and_6 (and_6_out, comparator_8_eq, comparator_9_eq, in_9);
  or or_2 (out_19, and_3_out, and_4_out, and_5_out, and_6_out);

  assign out_20 = out_19;

  // Other names for the same wires on the sheet: Branch = in_6; Bubble_f = out_17; Bubble_j = out_18;
  //   Bypass1[1:0] = out_13; Bypass2[1:0] = out_15; Bypass3[1:0] = out_14; Bypass4[1:0] = out_16; IR1[31:0] = in_3;
  //   JmpReg = in_7; Jump = in_8; Bubble = out_19; LoadUse = out_19; MemR = in_9; R1[4:0] = in_1; R1Src = in_12;
  //   R2_[4:0] = in_2; RegW2 = in_10; RegW3 = in_11; RW_2[4:0] = in_4; RW_3[4:0] = in_5
endmodule

module RD1 (
  input  [4:0] in_1,
  input  [4:0] in_2,
  input  [4:0] in_3,
  input  in_4,
  input  in_5,
  input  in_6,
  output [1:0] out_7
);

  wire and_2_out, and_5_out, comparator_1_eq, comparator_2_eq, comparator_3_eq, comparator_4_eq,
       comparator_5_eq, comparator_6_eq, comparator_7_eq, demultiplexer_1_out2, demultiplexer_1_out3,
       or_1_out, or_2_out;
  wire [1:0] and_3_out;
  wire [1:1] and_1_out;

  Comparator #(.width(5)) comparator_1 (.a(in_1), .b(in_2), .eq(comparator_1_eq));  // open: gt, lt
  Comparator #(.width(5)) comparator_2 (.a(in_1), .b({5{1'b0}}), .eq(comparator_2_eq));  // open: gt, lt
  Comparator #(.width(5)) comparator_3 (.a(in_1), .b(in_3), .eq(comparator_3_eq));  // open: gt, lt
  Comparator #(.width(5)) comparator_4 (.a(in_1), .b({5{1'b0}}), .eq(comparator_4_eq));  // open: gt, lt
  and and_1 (and_1_out[1], comparator_3_eq, ~comparator_4_eq, in_6);  // AND_Gate
  Demultiplexer #(.select(2), .enable("false")) demultiplexer_1 (
    .out2(demultiplexer_1_out2), .out3(demultiplexer_1_out3), .in(and_1_out[1]), .sel({and_1_out[1], in_4}));  // open: out0, out1
  and and_2 (and_2_out, in_5, comparator_1_eq, ~comparator_2_eq, ~in_4);  // AND_Gate
  or or_1 (or_1_out, and_2_out, demultiplexer_1_out3);
  or or_2 (or_2_out, demultiplexer_1_out3, demultiplexer_1_out2);
  and and_3 (and_3_out[0], or_1_out, ~demultiplexer_1_out2);  // AND_Gate
  and and_4 (and_3_out[1], ~and_2_out, or_2_out);  // AND_Gate
  Comparator #(.width(5)) comparator_5 (.a(in_2), .b(in_3), .eq(comparator_5_eq));  // open: gt, lt
  Comparator #(.width(5)) comparator_6 (.a(in_3), .b({5{1'b0}}), .eq(comparator_6_eq));  // open: gt, lt
  Comparator #(.width(5)) comparator_7 (.a(in_3), .b(in_1), .eq(comparator_7_eq));  // open: gt, lt
  and and_5 (and_5_out, comparator_5_eq, ~comparator_6_eq, comparator_7_eq);  // AND_Gate
  Multiplexer #(.width(2), .enable("false")) multiplexer_1 (.in0(and_3_out), .in1(2'b01), .out(out_7), .sel(and_5_out));

  // Other names for the same wires on the sheet: MemR = in_4; Bypass1[1:0] = out_7; R1[4:0] = in_1; RegW2 = in_5;
  //   RegW3 = in_6; RW_2[4:0] = in_2; RW_3[4:0] = in_3

  // Notes on the sheet:
  //   01
  //   10
  //   11
endmodule

module RD2 (
  input  [31:0] in_1,
  input  [4:0] in_2,
  input  [4:0] in_3,
  input  [4:0] in_4,
  input  in_5,
  input  in_6,
  input  in_7,
  output [1:0] out_8
);

  wire and_2_out, and_5_out, comparator_1_eq, comparator_2_eq, comparator_3_eq, comparator_4_eq,
       comparator_5_eq, comparator_6_eq, demultiplexer_1_out2, demultiplexer_1_out3, or_1_out, or_2_out;
  wire [1:0] and_3_out;
  wire [1:1] and_1_out;

  Comparator #(.width(32)) comparator_1 (.a(in_1), .b(32'hc), .eq(comparator_1_eq));  // open: gt, lt
  Comparator #(.width(5)) comparator_2 (.a(in_2), .b(in_4), .eq(comparator_2_eq));  // open: gt, lt
  Comparator #(.width(32)) comparator_3 (.a(in_1), .b(32'hc), .eq(comparator_3_eq));  // open: gt, lt
  Comparator #(.width(5)) comparator_4 (.a(in_3), .b(in_4), .eq(comparator_4_eq));  // open: gt, lt
  Demultiplexer #(.select(2), .enable("false")) demultiplexer_1 (
    .out2(demultiplexer_1_out2), .out3(demultiplexer_1_out3), .in(and_1_out[1]), .sel({and_1_out[1], in_5}));  // open: out0, out1
  and and_1 (and_1_out[1], comparator_3_eq, comparator_4_eq, in_7);
  and and_2 (and_2_out, in_6, comparator_1_eq, comparator_2_eq, ~in_5);  // AND_Gate
  or or_1 (or_1_out, and_2_out, demultiplexer_1_out3);
  or or_2 (or_2_out, demultiplexer_1_out3, demultiplexer_1_out2);
  and and_3 (and_3_out[0], or_1_out, ~demultiplexer_1_out2);  // AND_Gate
  and and_4 (and_3_out[1], ~and_2_out, or_2_out);  // AND_Gate
  Comparator #(.width(5)) comparator_5 (.a(in_2), .b(in_3), .eq(comparator_5_eq));  // open: gt, lt
  Comparator #(.width(5)) comparator_6 (.a(in_3), .b(in_4), .eq(comparator_6_eq));  // open: gt, lt
  Multiplexer #(.width(2), .enable("false")) multiplexer_1 (.in0(and_3_out), .in1(2'b01), .out(out_8), .sel(and_5_out));
  and and_5 (and_5_out, comparator_5_eq, comparator_6_eq);

  // Other names for the same wires on the sheet: MemR = in_5; IR1[31:0] = in_1; REG_num[4:0] = in_4; RegW2 = in_6;
  //   RegW3 = in_7; RW_2[4:0] = in_2; RW_3[4:0] = in_3

  // Notes on the sheet:
  //   01
  //   10
  //   11
endmodule
