// Logisim project Regfile.circ as structural Verilog: 3 circuits, main circuit main
module main (
  input  [4:0] Reg1_num,
  input  [4:0] Reg2,
  input  [4:0] Write_Reg_num,
  input  [31:0] Din,
  input  Write_Enable,
  input  Clock,
  output [31:0] Reg1,
  output [31:0] s0_Value,
  output [31:0] s1_Value,
  output [31:0] s2_Value,
  output [31:0] ra_Value,
  output [31:0] Reg2_2,
  output [31:0] out_13,
  output [31:0] out_14
);

  wire E0, E1, E2, E3, E4, E5, E6, E7, E8, E9, E10, E11, E12, E13, E14, E15, E16, E17, E18, E19, E20, E21,
       E22, E23, E24, E25, E26, E27, E28, E29, E30, E31;
  wire [31:0] _1, _3, _5, _6, _7, _8, _9, _10, _11, _12, _13, _14, _15, _16, _17, _18, _19, _20, _21, _22,
       _23, _24, _25, _26, _27, _28, _29, _30, _31;

  Register #(.width(32)) register_1 (.D(Din), .en(E16), .Q(_16), .clk(Clock));  // open: clr
  // Probe on Reg1_num
  Register #(.width(32)) register_2 (.D(Din), .en(E1), .Q(_1), .clk(Clock));  // open: clr
  Register #(.width(32)) register_3 (.D(Din), .en(E17), .Q(_17), .clk(Clock));  // open: clr
  Register #(.width(32)) register_4 (.D(Din), .en(E2), .Q(out_13), .clk(Clock));  // open: clr
  Register #(.width(32)) register_5 (.D(Din), .en(E18), .Q(_18), .clk(Clock));  // open: clr
  Demultiplexer #(.select(5)) demultiplexer_1 (
    .out0(E0), .out1(E1), .out2(E2), .out3(E3), .out4(E4), .out5(E5), .out6(E6), .out7(E7), .out8(E8),
    .out9(E9), .out10(E10), .out11(E11), .out12(E12), .out13(E13), .out14(E14), .out15(E15), .out16(E16),
    .out17(E17), .out18(E18), .out19(E19), .out20(E20), .out21(E21), .out22(E22), .out23(E23), .out24(E24),
    .out25(E25), .out26(E26), .out27(E27), .out28(E28), .out29(E29), .out30(E30), .out31(E31),
    .in(Write_Enable), .sel(Write_Reg_num));  // open: en
  Multiplexer #(.select(5), .width(32)) multiplexer_1 (
    .in0({32{1'b0}}), .in1(_1), .in2(out_13), .in3(_3), .in4(out_14), .in5(_5), .in6(_6), .in7(_7), .in8(_8),
    .in9(_9), .in10(_10), .in11(_11), .in12(_12), .in13(_13), .in14(_14), .in15(_15), .in16(_16), .in17(_17),
    .in18(_18), .in19(_19), .in20(_20), .in21(_21), .in22(_22), .in23(_23), .in24(_24), .in25(_25),
    .in26(_26), .in27(_27), .in28(_28), .in29(_29), .in30(_30), .in31(_31), .out(Reg1), .sel(Reg1_num));  // open: en
  Register #(.width(32)) register_6 (.D(Din), .en(E3), .Q(_3), .clk(Clock));  // open: clr
  Register #(.width(32)) register_7 (.D(Din), .en(E19), .Q(_19), .clk(Clock));  // open: clr
  Register #(.width(32)) register_8 (.D(Din), .en(E4), .Q(out_14), .clk(Clock));  // open: clr
  Register #(.width(32)) register_9 (.D(Din), .en(E20), .Q(_20), .clk(Clock));  // open: clr
  Register #(.width(32)) register_10 (.D(Din), .en(E5), .Q(_5), .clk(Clock));  // open: clr
  Register #(.width(32)) register_11 (.D(Din), .en(E21), .Q(_21), .clk(Clock));  // open: clr
  Register #(.width(32)) register_12 (.D(Din), .en(E6), .Q(_6), .clk(Clock));  // open: clr
  Register #(.width(32)) register_13 (.D(Din), .en(E22), .Q(_22), .clk(Clock));  // open: clr
  Register #(.width(32)) register_14 (.D(Din), .en(E7), .Q(_7), .clk(Clock));  // open: clr
  Register #(.width(32)) register_15 (.D(Din), .en(E23), .Q(_23), .clk(Clock));  // open: clr
  Register #(.width(32)) register_16 (.D(Din), .en(E8), .Q(_8), .clk(Clock));  // open: clr
  Register #(.width(32)) register_17 (.D(Din), .en(E24), .Q(_24), .clk(Clock));  // open: clr
  Multiplexer #(.select(5), .width(32)) multiplexer_2 (
    .in0({32{1'b0}}), .in1(_1), .in2(out_13), .in3(_3), .in4(out_14), .in5(_5), .in6(_6), .in7(_7), .in8(_8),
    .in9(_9), .in10(_10), .in11(_11), .in12(_12), .in13(_13), .in14(_14), .in15(_15), .in16(_16), .in17(_17),
    .in18(_18), .in19(_19), .in20(_20), .in21(_21), .in22(_22), .in23(_23), .in24(_24), .in25(_25),
    .in26(_26), .in27(_27), .in28(_28), .in29(_29), .in30(_30), .in31(_31), .out(Reg2_2), .sel(Reg2));  // open: en
  Register #(.width(32)) register_18 (.D(Din), .en(E9), .Q(_9), .clk(Clock));  // open: clr
  Register #(.width(32)) register_19 (.D(Din), .en(E25), .Q(_25), .clk(Clock));  // open: clr
  Register #(.width(32)) register_20 (.D(Din), .en(E10), .Q(_10), .clk(Clock));  // open: clr
  Register #(.width(32)) register_21 (.D(Din), .en(E26), .Q(_26), .clk(Clock));  // open: clr
  Register #(.width(32)) register_22 (.D(Din), .en(E11), .Q(_11), .clk(Clock));  // open: clr
  Register #(.width(32)) register_23 (.D(Din), .en(E27), .Q(_27), .clk(Clock));  // open: clr
  Register #(.width(32)) register_24 (.D(Din), .en(E12), .Q(_12), .clk(Clock));  // open: clr
  Register #(.width(32)) register_25 (.D(Din), .en(E28), .Q(_28), .clk(Clock));  // open: clr
  Register #(.width(32)) register_26 (.D(Din), .en(E13), .Q(_13), .clk(Clock));  // open: clr
  Register #(.width(32)) register_27 (.D(Din), .en(E29), .Q(_29), .clk(Clock));  // open: clr
  Register #(.width(32)) register_28 (.D(Din), .en(E14), .Q(_14), .clk(Clock));  // open: clr
  Register #(.width(32)) register_29 (.D(Din), .en(E30), .Q(_30), .clk(Clock));  // open: clr
  Register #(.width(32)) register_30 (.D(Din), .en(E15), .Q(_15), .clk(Clock));  // open: clr
  Register #(.width(32)) register_31 (.D(Din), .en(E31), .Q(_31), .clk(Clock));  // open: clr

  // Other names for the same wires on the sheet: _2[31:0] = out_13; _4[31:0] = out_14; clk = Clock;
  //   ra[31:0] = ra_Value; reg2_num[4:0] = Reg2; reg2_t[31:0] = Reg2_2; s0[31:0] = s0_Value; s1[31:0] = s1_Value;
  //   s2[31:0] = s2_Value; WE = Write_Enable; write_data[31:0] = Din

  // Notes on the sheet:
  //   输入引脚
  //   输出引脚
  //   Debug引脚，便于观测寄存器值
  //   请勿修改引脚以及封装，直接使用隧道连接电路
endmodule

module test (
);

  wire undriven;

  main main_1 (.Clock(undriven));  // open: Reg1_num, Reg2, Write_Reg_num, Din, Write_Enable, Reg1, Reg2_2, s0_Value, s1_Value, s2_Value, ra_Value, out_13, out_14
endmodule

module cal (
);

  wire and_2_out, clock, clock_1_out, d_ff_1_qn, max_flag, mux_choose, not_1_out, not_2_out;
  wire [4:0] write_reg;
  wire [4:1] counter_1_q;
  wire [5:0] adder_2_out, counter_2_q, input_addr;
  wire [31:0] load_value, main_1_reg1, main_1_reg2_2, multiplexer_1_out, temp_ans;

  Clock clock_1 (.out(clock_1_out));
  not not_1 (not_1_out, max_flag);
  not not_2 (not_2_out, mux_choose);
  D_Flip_Flop d_ff_1 (
    .clk(clock_1_out), .D(max_flag), .Qn(d_ff_1_qn), .preset(1'b0), .en(1'b1), .reset(1'b0));  // open: Q
  and and_1 (clock, clock_1_out, not_1_out);
  RAM #(.addrWidth(6), .dataWidth(32), .bus("separate")) ram_1 (
    .addr(input_addr), .din(temp_ans), .data(load_value), .str(1'b1), .sel(1'b1), .clk(not_2_out), .ld(1'b1),
    .clr(1'b0));
  Counter #(.width(5), .max('h1)) counter_1 (
    .load(1'b0), .count(1'b1), .Q({counter_1_q, mux_choose}), .clk(and_2_out));  // open: D, carry, clr
  and and_2 (and_2_out, clock_1_out, d_ff_1_qn);
  Adder #(.width(5)) adder_1 (.a({counter_1_q, mux_choose}), .b(5'b00001), .out(write_reg));  // open: cin, cout
  Hex_Digit_Display hex_digit_display_1 (.value(temp_ans[31:28]));  // open: dp
  Hex_Digit_Display hex_digit_display_2 (.value(temp_ans[27:24]));  // open: dp
  Hex_Digit_Display hex_digit_display_3 (.value(temp_ans[23:20]));  // open: dp
  Multiplexer #(.width(32), .enable("false")) multiplexer_1 (
    .in0(load_value), .in1(temp_ans), .out(multiplexer_1_out), .sel(mux_choose));
  Hex_Digit_Display hex_digit_display_4 (.value(temp_ans[19:16]));  // open: dp
  Hex_Digit_Display hex_digit_display_5 (.value(temp_ans[15:12]));  // open: dp
  main main_1 (
    .Reg1_num(5'b00001), .Reg2(5'b00010), .Write_Reg_num(write_reg), .Din(multiplexer_1_out),
    .Write_Enable(1'b1), .Clock(clock), .Reg1(main_1_reg1), .Reg2_2(main_1_reg2_2), .out_14(main_1_reg1));  // open: s0_Value, s1_Value, s2_Value, ra_Value, out_13
  Hex_Digit_Display hex_digit_display_6 (.value(temp_ans[7:4]));  // open: dp
  Hex_Digit_Display hex_digit_display_7 (.value(temp_ans[11:8]));  // open: dp
  ALU alu_1 (
    .AluOP(4'b0101), .X(main_1_reg1), .Result(temp_ans), .Y(main_1_reg2_2));  // open: Equal, Signed_Overflow_350b0444, Result_2_406f29fe, UnSigned_Overflow_28bd2ab2
  Counter #(.width(6), .max('h20), .ongoal("stay")) counter_2 (
    .load(1'b0), .count(1'b1), .Q(counter_2_q), .carry(max_flag), .clk(mux_choose));  // open: D, clr
  Hex_Digit_Display hex_digit_display_8 (.value(temp_ans[3:0]));  // open: dp
  Multiplexer #(.width(6), .enable("false")) multiplexer_2 (
    .in0(counter_2_q), .in1(adder_2_out), .out(input_addr), .sel(mux_choose));
  Adder #(.width(6)) adder_2 (.a(counter_2_q), .b(6'b011111), .out(adder_2_out));  // open: cin, cout
endmodule
